// Digital circuit Template.dig as structural Verilog
module Template (
  input  T,
  input  Clear,
  input  Clock,
  output Q,
  output Q_2
);

  wire and_1_out, nand_1_out, nand_2_out, nand_3_out, nand_4_out, not_1_out, xor_1_out;

  xor xor_1 (xor_1_out, Q, T);
  not not_1 (not_1_out, Clear);
  and and_1 (and_1_out, not_1_out, xor_1_out);
  nand nand_1 (nand_1_out, nand_4_out, nand_2_out);
  nand nand_2 (nand_2_out, nand_1_out, Clock);
  nand nand_3 (nand_3_out, nand_2_out, Clock, nand_4_out);
  nand nand_4 (nand_4_out, nand_3_out, and_1_out);
  nand nand_5 (Q, nand_2_out, Q_2);
  nand nand_6 (Q_2, Q, nand_3_out);
endmodule
