// Digital circuit THISISTHEREALESTSHITBROTrustMeBRO.dig as structural Verilog
module THISISTHEREALESTSHITBROTrustMeBRO (
  input  reset,
  input  clock,
  input  P5,
  input  P10,
  input  P20,
  input  Pcoffee,
  input  Ptea,
  input  Pchange,
  input  Pnext,
  output CoffeeOut,
  output TeaOut,
  output [1:0] Change5,
  output [1:0] Change10,
  output [1:0] Change20,
  output [5:0] Balance
);

  wire AddChange5, AddChange10, AddChange20, and_1_out, and_2_out, and_3_out, and_4_out, and_5_out,
       and_6_out, and_7_out, and_8_out, and_9_out, and_10_out, and_11_out, and_12_out, and_13_out,
       and_14_out, and_20_out, and_21_out, and_22_out, Balance_gt__eq_5, Balance_gt__eq_10,
       Balance_gt__eq_20, Balance_gt__eq_25, Balance_lt__eq_30, Balance_lt__eq_40, Balance_lt__eq_45,
       canAdd5, canAdd10, canAdd20, canPayCoffee, canPayTea, ChangePrep, d_ff_1_q, d_ff_3_q, d_ff_4_q,
       d_ff_5_q, d_ff_6_q, d_ff_7_q, d_ff_8_q, d_ff_9_q, d_ff_10_q, d_ff_11_q, d_ff_12_q, d_ff_13_q,
       demultiplexer_1_out_4, demultiplexer_1_out_5, driverinvsel_1_out, driverinvsel_2_out,
       driverinvsel_3_out, driverinvsel_4_out, multiplexer_1_out, multiplexer_2_out, multiplexer_3_out,
       multiplexer_4_out, NextOrder, not_1_out, not_2_out, or_1_out, or_2_out, or_3_out, or_4_out, or_5_out,
       or_6_out, or_7_out, or_8_out, or_9_out, or_10_out, or_11_out, or_12_out, or_13_out, or_14_out,
       or_15_out, or_16_out, or_17_out, or_18_out, or_19_out, Pchange_t, Pnext_t, R;
  wire [3:0] State;
  wire [5:0] d_ff_15_q, multiplexer_5_out;
  wire [6:0] multiplexer_6_out;
  wire [6:6] add_1_s;

  and and_1 (and_1_out, Pchange, or_1_out);
  or or_1 (or_1_out, d_ff_1_q, Pchange_t);
  and and_2 (and_2_out, Pchange, ~d_ff_1_q, ~Pchange_t);  // And
  and and_3 (and_3_out, P5, or_2_out);
  or or_2 (or_2_out, d_ff_3_q, d_ff_4_q);
  and and_4 (and_4_out, P5, ~d_ff_3_q, ~d_ff_4_q);  // And
  and and_5 (and_5_out, P10, or_3_out);
  or or_3 (or_3_out, d_ff_5_q, d_ff_6_q);
  and and_6 (and_6_out, P10, ~d_ff_5_q, ~d_ff_6_q);  // And
  and and_7 (and_7_out, P20, or_4_out);
  or or_4 (or_4_out, d_ff_7_q, d_ff_8_q);
  and and_8 (and_8_out, P20, ~d_ff_7_q, ~d_ff_8_q);  // And
  and and_9 (and_9_out, Pcoffee, or_5_out);
  or or_5 (or_5_out, d_ff_9_q, d_ff_10_q);
  and and_10 (and_10_out, Pcoffee, ~d_ff_9_q, ~d_ff_10_q);  // And
  and and_11 (and_11_out, Ptea, or_6_out);
  or or_6 (or_6_out, d_ff_11_q, d_ff_12_q);
  and and_12 (and_12_out, Ptea, ~d_ff_11_q, ~d_ff_12_q);  // And
  and and_13 (and_13_out, Pnext, or_7_out);
  or or_7 (or_7_out, d_ff_13_q, Pnext_t);
  and and_14 (and_14_out, Pnext, ~d_ff_13_q, ~Pnext_t);  // And
  D_FF d_ff_1 (.D(and_1_out), .C(clock), .Q(d_ff_1_q));  // open: nQ
  D_FF d_ff_2 (.D(and_2_out), .C(clock), .Q(Pchange_t));  // open: nQ
  D_FF d_ff_3 (.D(and_3_out), .C(clock), .Q(d_ff_3_q));  // open: nQ
  D_FF d_ff_4 (.D(and_4_out), .C(clock), .Q(d_ff_4_q));  // open: nQ
  D_FF d_ff_5 (.D(and_5_out), .C(clock), .Q(d_ff_5_q));  // open: nQ
  D_FF d_ff_6 (.D(and_6_out), .C(clock), .Q(d_ff_6_q));  // open: nQ
  D_FF d_ff_7 (.D(and_7_out), .C(clock), .Q(d_ff_7_q));  // open: nQ
  D_FF d_ff_8 (.D(and_8_out), .C(clock), .Q(d_ff_8_q));  // open: nQ
  D_FF d_ff_9 (.D(and_9_out), .C(clock), .Q(d_ff_9_q));  // open: nQ
  D_FF d_ff_10 (.D(and_10_out), .C(clock), .Q(d_ff_10_q));  // open: nQ
  D_FF d_ff_11 (.D(and_11_out), .C(clock), .Q(d_ff_11_q));  // open: nQ
  D_FF d_ff_12 (.D(and_12_out), .C(clock), .Q(d_ff_12_q));  // open: nQ
  D_FF d_ff_13 (.D(and_13_out), .C(clock), .Q(d_ff_13_q));  // open: nQ
  D_FF d_ff_14 (.D(and_14_out), .C(clock), .Q(Pnext_t));  // open: nQ
  and and_15 (canAdd5, d_ff_4_q, Balance_lt__eq_45);
  and and_16 (canAdd10, d_ff_6_q, Balance_lt__eq_40);
  and and_17 (canAdd20, d_ff_8_q, Balance_lt__eq_30);
  and and_18 (canPayCoffee, d_ff_10_q, Balance_gt__eq_25);
  and and_19 (canPayTea, d_ff_12_q, Balance_gt__eq_20);
  and and_20 (and_20_out, ~Balance_gt__eq_10, Balance_gt__eq_5);  // And
  and and_21 (and_21_out, ~Balance_gt__eq_20, Balance_gt__eq_10);  // And
  and and_22 (and_22_out, ~Balance_gt__eq_20, Balance_gt__eq_10);  // And
  or or_8 (or_8_out, Pchange_t, reset);
  Multiplexer #(.Selector_Bits(4)) multiplexer_1 (
    .sel(State), .in_0(or_8_out), .in_1(1'b0), .in_2(1'b0), .in_3(1'b0), .in_4(1'b0), .in_5(1'b0),
    .in_6(or_9_out), .in_7(1'b0), .in_8(1'b1), .in_9(or_10_out), .in_10(1'b1), .in_11(1'b1), .in_12(1'b1),
    .in_13(1'b0), .in_14(1'b0), .in_15(1'b0), .out(multiplexer_1_out));
  or or_9 (or_9_out, Pchange_t, reset);
  or or_10 (or_10_out, Balance_gt__eq_5, reset);
  or or_11 (or_11_out, canPayCoffee, canPayTea, reset);
  Multiplexer #(.Selector_Bits(4)) multiplexer_2 (
    .sel(State), .in_0(or_11_out), .in_1(1'b0), .in_2(1'b0), .in_3(1'b0), .in_4(1'b1), .in_5(1'b1),
    .in_6(not_1_out), .in_7(1'b0), .in_8(1'b0), .in_9(or_12_out), .in_10(1'b0), .in_11(1'b0), .in_12(1'b0),
    .in_13(1'b0), .in_14(1'b0), .in_15(1'b0), .out(multiplexer_2_out));
  not not_1 (not_1_out, Pchange_t);
  or or_12 (or_12_out, and_20_out, reset);
  or or_13 (or_13_out, canAdd20, canAdd10, reset);
  Multiplexer #(.Selector_Bits(4)) multiplexer_3 (
    .sel(State), .in_0(or_13_out), .in_1(1'b0), .in_2(1'b0), .in_3(1'b0), .in_4(1'b1), .in_5(1'b1),
    .in_6(not_2_out), .in_7(1'b0), .in_8(1'b0), .in_9(or_14_out), .in_10(1'b0), .in_11(1'b0), .in_12(1'b0),
    .in_13(1'b0), .in_14(1'b0), .in_15(1'b0), .out(multiplexer_3_out));
  not not_2 (not_2_out, Pchange_t);
  or or_14 (or_14_out, Balance_gt__eq_20, and_21_out, reset);
  or or_15 (or_15_out, canAdd5, canAdd20, canPayCoffee, reset);
  Multiplexer #(.Selector_Bits(4)) multiplexer_4 (
    .sel(State), .in_0(or_15_out), .in_1(1'b0), .in_2(1'b0), .in_3(1'b0), .in_4(1'b0), .in_5(1'b0),
    .in_6(or_16_out), .in_7(1'b0), .in_8(1'b1), .in_9(or_17_out), .in_10(1'b1), .in_11(1'b1), .in_12(1'b1),
    .in_13(1'b0), .in_14(1'b0), .in_15(1'b0), .out(multiplexer_4_out));
  or or_16 (or_16_out, Pnext_t, reset);
  or or_17 (or_17_out, and_22_out, reset);
  D_FF Q3 (.D(multiplexer_1_out), .C(clock), .Q(State[3]));  // open: nQ
  D_FF Q2 (.D(multiplexer_2_out), .C(clock), .Q(State[2]));  // open: nQ
  D_FF Q1 (.D(multiplexer_3_out), .C(clock), .Q(State[1]));  // open: nQ
  D_FF Q0 (.D(multiplexer_4_out), .C(clock), .Q(State[0]));  // open: nQ
  Demultiplexer #(.Selector_Bits(4)) demultiplexer_1 (
    .sel(State), .in(1'b1), .out_4(demultiplexer_1_out_4), .out_5(demultiplexer_1_out_5), .out_7(NextOrder),
    .out_8(ChangePrep), .out_10(AddChange20), .out_11(AddChange10), .out_12(AddChange5), .out_15(R));  // open: out_0, out_1, out_2, out_3, out_6, out_9, out_13, out_14
  or or_18 (or_18_out, R, ChangePrep, NextOrder);
  Multiplexer #(.Bits(6)) multiplexer_5 (.sel(R), .in_0(Balance), .in_1({6{1'b0}}), .out(multiplexer_5_out));
  D_FF #(.Bits(6)) d_ff_15 (.D(multiplexer_5_out), .C(clock), .Q(d_ff_15_q));  // open: nQ
  assign driverinvsel_1_out = ~demultiplexer_1_out_4 ? TeaOut : 1'bz;  // DriverInvSel driverinvsel_1
  assign driverinvsel_1_out = demultiplexer_1_out_4 ? 1'b1 : 1'bz;  // Driver driver_1
  assign driverinvsel_2_out = ~demultiplexer_1_out_5 ? CoffeeOut : 1'bz;  // DriverInvSel driverinvsel_2
  assign driverinvsel_2_out = demultiplexer_1_out_5 ? 1'b1 : 1'bz;  // Driver driver_2
  assign driverinvsel_3_out = ~or_18_out ? driverinvsel_1_out : 1'bz;  // DriverInvSel driverinvsel_3
  assign driverinvsel_3_out = or_18_out ? 1'b0 : 1'bz;  // Driver driver_3
  assign driverinvsel_4_out = ~or_18_out ? driverinvsel_2_out : 1'bz;  // DriverInvSel driverinvsel_4
  assign driverinvsel_4_out = or_18_out ? 1'b0 : 1'bz;  // Driver driver_4
  or or_19 (or_19_out, R, ChangePrep);
  Multiplexer #(.Selector_Bits(4), .Bits(7)) multiplexer_6 (
    .sel(State), .in_0({7{1'b0}}), .in_1(7'b0000101), .in_2(7'b0001010), .in_3(7'b0010100),
    .in_4(7'b1101100), .in_5(7'b1100111), .in_6({7{1'b0}}), .in_7({7{1'b0}}), .in_8({7{1'b0}}),
    .in_9({7{1'b0}}), .in_10(7'b1101100), .in_11(7'b1110110), .in_12(7'b1111011), .in_13({7{1'b0}}),
    .in_14({7{1'b0}}), .in_15({7{1'b0}}), .out(multiplexer_6_out));
  D_FF d_ff_16 (.D(driverinvsel_3_out), .C(clock), .Q(TeaOut));  // open: nQ
  D_FF d_ff_17 (.D(driverinvsel_4_out), .C(clock), .Q(CoffeeOut));  // open: nQ
  Add #(.Bits(7)) add_1 (
    .a({1'b0, d_ff_15_q}), .b(multiplexer_6_out), .c_i(1'b0), .s({add_1_s[6], Balance}));  // open: c_o
  Counter #(.Bits(2)) counter_1 (.en(AddChange20), .C(clock), .clr(or_19_out), .out(Change20));  // open: ovf
  Counter #(.Bits(2)) counter_2 (.en(AddChange10), .C(clock), .clr(or_19_out), .out(Change10));  // open: ovf
  Counter #(.Bits(2)) counter_3 (.en(AddChange5), .C(clock), .clr(or_19_out), .out(Change5));  // open: ovf
  Comparator #(.Bits(6)) comparator_1 (.a(Balance), .b(6'b101110), .lt(Balance_lt__eq_45));  // open: gt, eq
  Comparator #(.Bits(6)) comparator_2 (.a(Balance), .b(6'b101001), .lt(Balance_lt__eq_40));  // open: gt, eq
  Comparator #(.Bits(6)) comparator_3 (.a(Balance), .b(6'b011111), .lt(Balance_lt__eq_30));  // open: gt, eq
  Comparator #(.Bits(6)) comparator_4 (.a(Balance), .b(6'b010011), .gt(Balance_gt__eq_20));  // open: eq, lt
  Comparator #(.Bits(6)) comparator_5 (.a(Balance), .b(6'b011000), .gt(Balance_gt__eq_25));  // open: eq, lt
  Comparator #(.Bits(6)) comparator_6 (.a(Balance), .b(6'b001001), .gt(Balance_gt__eq_10));  // open: eq, lt
  Comparator #(.Bits(6)) comparator_7 (.a(Balance), .b(6'b000100), .gt(Balance_gt__eq_5));  // open: eq, lt
endmodule

/* Test case TC1:
clock reset P5 P10 P20 Pcoffee Ptea Pchange Pnext Balance CoffeeOut TeaOut Change5 Change10 Change20
0 1 0 0 0 0 0 0 0 x x x x x x
1 1 0 0 0 0 0 0 0 0 0 0 0 0 0
0 0 1 0 0 0 0 0 0 0 0 0 0 0 0
1 0 1 0 0 0 0 0 0 0 0 0 0 0 0
0 0 0 0 0 0 0 0 0 x x x x x x
1 0 0 0 0 0 0 0 0 x x x x x x
0 0 0 0 0 0 0 0 0 x x x x x x
1 0 0 0 0 0 0 0 0 x x x x x x
0 0 0 0 0 0 0 0 0 x x x x x x
1 0 0 0 0 0 0 0 0 x x x x x x
0 0 0 0 0 0 0 0 0 x x x x x x
1 0 0 0 0 0 0 0 0 x x x x x x
0 0 0 0 0 0 0 0 0 x x x x x x
1 0 0 0 0 0 0 0 0 x x x x x x
0 0 0 0 0 0 0 0 0 x x x x x x
1 0 0 0 0 0 0 0 0 x x x x x x
0 0 0 0 0 0 0 0 0 x x x x x x
1 0 0 0 0 0 0 0 0 x x x x x x
0 0 0 0 0 0 0 0 0 x x x x x x
1 0 0 0 0 0 0 0 0 x x x x x x
0 0 0 0 0 0 0 0 0 x x x x x x
1 0 0 0 0 0 0 0 0 x x x x x x
0 0 0 0 0 0 0 0 0 x x x x x x
1 0 0 0 0 0 0 0 0 x x x x x x
0 0 0 0 0 0 0 0 0 x x x x x x
1 0 0 0 0 0 0 0 0 x x x x x x
0 0 0 0 0 0 0 0 0 x x x x x x
1 0 0 0 0 0 0 0 0 x x x x x x
0 0 0 0 0 0 0 0 0 x x x x x x
1 0 0 0 0 0 0 0 0 x x x x x x
0 0 0 0 0 0 0 0 0 x x x x x x
1 0 0 0 0 0 0 0 0 x x x x x x
0 0 0 0 0 0 0 0 0 x x x x x x
1 0 0 0 0 0 0 0 0 x x x x x x
0 0 0 0 0 0 0 0 0 x x x x x x
1 0 0 0 0 0 0 0 0 x x x x x x
0 0 0 0 0 0 0 0 0 x x x x x x
1 0 0 0 0 0 0 0 0 x x x x x x
0 0 0 0 0 0 0 0 0 x x x x x x
1 0 0 0 0 0 0 0 0 x x x x x x
0 0 0 0 0 0 0 0 0 x x x x x x
1 0 0 0 0 0 0 0 0 x x x x x x
0 0 0 0 0 0 0 0 0 x x x x x x
1 0 0 0 0 0 0 0 0 x x x x x x
0 0 0 0 0 0 0 0 0 5 0 0 0 0 0
1 0 0 0 0 0 0 0 0 5 0 0 0 0 0
0 0 0 1 0 0 0 0 0 5 0 0 0 0 0
1 0 0 1 0 0 0 0 0 5 0 0 0 0 0
0 0 0 0 0 0 0 0 0 x x x x x x
1 0 0 0 0 0 0 0 0 x x x x x x
0 0 0 0 0 0 0 0 0 x x x x x x
1 0 0 0 0 0 0 0 0 x x x x x x
0 0 0 0 0 0 0 0 0 x x x x x x
1 0 0 0 0 0 0 0 0 x x x x x x
0 0 0 0 0 0 0 0 0 x x x x x x
1 0 0 0 0 0 0 0 0 x x x x x x
0 0 0 0 0 0 0 0 0 x x x x x x
1 0 0 0 0 0 0 0 0 x x x x x x
0 0 0 0 0 0 0 0 0 x x x x x x
1 0 0 0 0 0 0 0 0 x x x x x x
0 0 0 0 0 0 0 0 0 x x x x x x
1 0 0 0 0 0 0 0 0 x x x x x x
0 0 0 0 0 0 0 0 0 x x x x x x
1 0 0 0 0 0 0 0 0 x x x x x x
0 0 0 0 0 0 0 0 0 x x x x x x
1 0 0 0 0 0 0 0 0 x x x x x x
0 0 0 0 0 0 0 0 0 x x x x x x
1 0 0 0 0 0 0 0 0 x x x x x x
0 0 0 0 0 0 0 0 0 x x x x x x
1 0 0 0 0 0 0 0 0 x x x x x x
0 0 0 0 0 0 0 0 0 x x x x x x
1 0 0 0 0 0 0 0 0 x x x x x x
0 0 0 0 0 0 0 0 0 x x x x x x
1 0 0 0 0 0 0 0 0 x x x x x x
0 0 0 0 0 0 0 0 0 x x x x x x
1 0 0 0 0 0 0 0 0 x x x x x x
0 0 0 0 0 0 0 0 0 x x x x x x
1 0 0 0 0 0 0 0 0 x x x x x x
0 0 0 0 0 0 0 0 0 x x x x x x
1 0 0 0 0 0 0 0 0 x x x x x x
0 0 0 0 0 0 0 0 0 x x x x x x
1 0 0 0 0 0 0 0 0 x x x x x x
0 0 0 0 0 0 0 0 0 x x x x x x
1 0 0 0 0 0 0 0 0 x x x x x x
0 0 0 0 0 0 0 0 0 x x x x x x
1 0 0 0 0 0 0 0 0 x x x x x x
0 0 0 0 0 0 0 0 0 x x x x x x
1 0 0 0 0 0 0 0 0 x x x x x x
0 0 0 0 0 0 0 0 0 15 0 0 0 0 0
1 0 0 0 0 0 0 0 0 15 0 0 0 0 0
0 0 0 0 1 0 0 0 0 15 0 0 0 0 0
1 0 0 0 1 0 0 0 0 15 0 0 0 0 0
0 0 0 0 0 0 0 0 0 x x x x x x
1 0 0 0 0 0 0 0 0 x x x x x x
0 0 0 0 0 0 0 0 0 x x x x x x
1 0 0 0 0 0 0 0 0 x x x x x x
0 0 0 0 0 0 0 0 0 x x x x x x
1 0 0 0 0 0 0 0 0 x x x x x x
0 0 0 0 0 0 0 0 0 x x x x x x
1 0 0 0 0 0 0 0 0 x x x x x x
0 0 0 0 0 0 0 0 0 x x x x x x
1 0 0 0 0 0 0 0 0 x x x x x x
0 0 0 0 0 0 0 0 0 x x x x x x
1 0 0 0 0 0 0 0 0 x x x x x x
0 0 0 0 0 0 0 0 0 x x x x x x
1 0 0 0 0 0 0 0 0 x x x x x x
0 0 0 0 0 0 0 0 0 x x x x x x
1 0 0 0 0 0 0 0 0 x x x x x x
0 0 0 0 0 0 0 0 0 x x x x x x
1 0 0 0 0 0 0 0 0 x x x x x x
0 0 0 0 0 0 0 0 0 x x x x x x
1 0 0 0 0 0 0 0 0 x x x x x x
0 0 0 0 0 0 0 0 0 x x x x x x
1 0 0 0 0 0 0 0 0 x x x x x x
0 0 0 0 0 0 0 0 0 x x x x x x
1 0 0 0 0 0 0 0 0 x x x x x x
0 0 0 0 0 0 0 0 0 x x x x x x
1 0 0 0 0 0 0 0 0 x x x x x x
0 0 0 0 0 0 0 0 0 x x x x x x
1 0 0 0 0 0 0 0 0 x x x x x x
0 0 0 0 0 0 0 0 0 x x x x x x
1 0 0 0 0 0 0 0 0 x x x x x x
0 0 0 0 0 0 0 0 0 x x x x x x
1 0 0 0 0 0 0 0 0 x x x x x x
0 0 0 0 0 0 0 0 0 x x x x x x
1 0 0 0 0 0 0 0 0 x x x x x x
0 0 0 0 0 0 0 0 0 x x x x x x
1 0 0 0 0 0 0 0 0 x x x x x x
0 0 0 0 0 0 0 0 0 x x x x x x
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*/

/* Test case TC2:
clock reset P5 P10 P20 Pcoffee Ptea Pchange Pnext Balance CoffeeOut TeaOut Change5 Change10 Change20
0 1 0 0 0 0 0 0 0 x x x x x x
1 1 0 0 0 0 0 0 0 0 0 0 0 0 0
0 0 0 0 0 1 0 0 0 0 0 0 0 0 0
1 0 0 0 0 1 0 0 0 0 0 0 0 0 0
0 0 0 0 0 0 0 0 0 x x x x x x
1 0 0 0 0 0 0 0 0 x x x x x x
0 0 0 0 0 0 0 0 0 x x x x x x
1 0 0 0 0 0 0 0 0 x x x x x x
0 0 0 0 0 0 0 0 0 x x x x x x
1 0 0 0 0 0 0 0 0 x x x x x x
0 0 0 0 0 0 0 0 0 x x x x x x
1 0 0 0 0 0 0 0 0 x x x x x x
0 0 0 0 0 0 0 0 0 x x x x x x
1 0 0 0 0 0 0 0 0 x x x x x x
0 0 0 0 0 0 0 0 0 x x x x x x
1 0 0 0 0 0 0 0 0 x x x x x x
0 0 0 0 0 0 0 0 0 x x x x x x
1 0 0 0 0 0 0 0 0 x x x x x x
0 0 0 0 0 0 0 0 0 x x x x x x
1 0 0 0 0 0 0 0 0 x x x x x x
0 0 0 0 0 0 0 0 0 x x x x x x
1 0 0 0 0 0 0 0 0 x x x x x x
0 0 0 0 0 0 0 0 0 x x x x x x
1 0 0 0 0 0 0 0 0 x x x x x x
0 0 0 0 0 0 0 0 0 x x x x x x
1 0 0 0 0 0 0 0 0 x x x x x x
0 0 0 0 0 0 0 0 0 x x x x x x
1 0 0 0 0 0 0 0 0 x x x x x x
0 0 0 0 0 0 0 0 0 x x x x x x
1 0 0 0 0 0 0 0 0 x x x x x x
0 0 0 0 0 0 0 0 0 x x x x x x
1 0 0 0 0 0 0 0 0 x x x x x x
0 0 0 0 0 0 0 0 0 x x x x x x
1 0 0 0 0 0 0 0 0 x x x x x x
0 0 0 0 0 0 0 0 0 x x x x x x
1 0 0 0 0 0 0 0 0 x x x x x x
0 0 0 0 0 0 0 0 0 x x x x x x
1 0 0 0 0 0 0 0 0 x x x x x x
0 0 0 0 0 0 0 0 0 x x x x x x
1 0 0 0 0 0 0 0 0 x x x x x x
0 0 0 0 0 0 0 0 0 x x x x x x
1 0 0 0 0 0 0 0 0 x x x x x x
0 0 0 0 0 0 0 0 0 x x x x x x
1 0 0 0 0 0 0 0 0 x x x x x x
0 0 0 0 0 0 0 0 0 0 0 0 0 0 0
1 0 0 0 0 0 0 0 0 0 0 0 0 0 0
0 0 0 0 0 0 1 0 0 0 0 0 0 0 0
1 0 0 0 0 0 1 0 0 0 0 0 0 0 0
0 0 0 0 0 0 0 0 0 x x x x x x
1 0 0 0 0 0 0 0 0 x x x x x x
0 0 0 0 0 0 0 0 0 x x x x x x
1 0 0 0 0 0 0 0 0 x x x x x x
0 0 0 0 0 0 0 0 0 x x x x x x
1 0 0 0 0 0 0 0 0 x x x x x x
0 0 0 0 0 0 0 0 0 x x x x x x
1 0 0 0 0 0 0 0 0 x x x x x x
0 0 0 0 0 0 0 0 0 x x x x x x
1 0 0 0 0 0 0 0 0 x x x x x x
0 0 0 0 0 0 0 0 0 x x x x x x
1 0 0 0 0 0 0 0 0 x x x x x x
0 0 0 0 0 0 0 0 0 x x x x x x
1 0 0 0 0 0 0 0 0 x x x x x x
0 0 0 0 0 0 0 0 0 x x x x x x
1 0 0 0 0 0 0 0 0 x x x x x x
0 0 0 0 0 0 0 0 0 x x x x x x
1 0 0 0 0 0 0 0 0 x x x x x x
0 0 0 0 0 0 0 0 0 x x x x x x
1 0 0 0 0 0 0 0 0 x x x x x x
0 0 0 0 0 0 0 0 0 x x x x x x
1 0 0 0 0 0 0 0 0 x x x x x x
0 0 0 0 0 0 0 0 0 x x x x x x
1 0 0 0 0 0 0 0 0 x x x x x x
0 0 0 0 0 0 0 0 0 x x x x x x
1 0 0 0 0 0 0 0 0 x x x x x x
0 0 0 0 0 0 0 0 0 x x x x x x
1 0 0 0 0 0 0 0 0 x x x x x x
0 0 0 0 0 0 0 0 0 x x x x x x
1 0 0 0 0 0 0 0 0 x x x x x x
0 0 0 0 0 0 0 0 0 x x x x x x
1 0 0 0 0 0 0 0 0 x x x x x x
0 0 0 0 0 0 0 0 0 x x x x x x
1 0 0 0 0 0 0 0 0 x x x x x x
0 0 0 0 0 0 0 0 0 x x x x x x
1 0 0 0 0 0 0 0 0 x x x x x x
0 0 0 0 0 0 0 0 0 x x x x x x
1 0 0 0 0 0 0 0 0 x x x x x x
0 0 0 0 0 0 0 0 0 x x x x x x
1 0 0 0 0 0 0 0 0 x x x x x x
0 0 0 0 0 0 0 0 0 0 0 0 0 0 0
1 0 0 0 0 0 0 0 0 0 0 0 0 0 0
0 0 0 0 1 0 0 0 0 0 0 0 0 0 0
1 0 0 0 1 0 0 0 0 0 0 0 0 0 0
0 0 0 0 0 0 0 0 0 x x x x x x
1 0 0 0 0 0 0 0 0 x x x x x x
0 0 0 0 0 0 0 0 0 x x x x x x
1 0 0 0 0 0 0 0 0 x x x x x x
0 0 0 0 0 0 0 0 0 x x x x x x
1 0 0 0 0 0 0 0 0 x x x x x x
0 0 0 0 0 0 0 0 0 x x x x x x
1 0 0 0 0 0 0 0 0 x x x x x x
0 0 0 0 0 0 0 0 0 x x x x x x
1 0 0 0 0 0 0 0 0 x x x x x x
0 0 0 0 0 0 0 0 0 x x x x x x
1 0 0 0 0 0 0 0 0 x x x x x x
0 0 0 0 0 0 0 0 0 x x x x x x
1 0 0 0 0 0 0 0 0 x x x x x x
0 0 0 0 0 0 0 0 0 x x x x x x
1 0 0 0 0 0 0 0 0 x x x x x x
0 0 0 0 0 0 0 0 0 x x x x x x
1 0 0 0 0 0 0 0 0 x x x x x x
0 0 0 0 0 0 0 0 0 x x x x x x
1 0 0 0 0 0 0 0 0 x x x x x x
0 0 0 0 0 0 0 0 0 x x x x x x
1 0 0 0 0 0 0 0 0 x x x x x x
0 0 0 0 0 0 0 0 0 x x x x x x
1 0 0 0 0 0 0 0 0 x x x x x x
0 0 0 0 0 0 0 0 0 x x x x x x
1 0 0 0 0 0 0 0 0 x x x x x x
0 0 0 0 0 0 0 0 0 x x x x x x
1 0 0 0 0 0 0 0 0 x x x x x x
0 0 0 0 0 0 0 0 0 x x x x x x
1 0 0 0 0 0 0 0 0 x x x x x x
0 0 0 0 0 0 0 0 0 x x x x x x
1 0 0 0 0 0 0 0 0 x x x x x x
0 0 0 0 0 0 0 0 0 x x x x x x
1 0 0 0 0 0 0 0 0 x x x x x x
0 0 0 0 0 0 0 0 0 x x x x x x
1 0 0 0 0 0 0 0 0 x x x x x x
0 0 0 0 0 0 0 0 0 x x x x x x
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*/

/* Test case TC3:
clock reset P5 P10 P20 Pcoffee Ptea Pchange Pnext Balance CoffeeOut TeaOut Change5 Change10 Change20
0 1 0 0 0 0 0 0 0 x x x x x x
1 1 0 0 0 0 0 0 0 0 0 0 0 0 0
0 0 1 0 0 0 0 0 0 0 0 0 0 0 0
1 0 1 0 0 0 0 0 0 0 0 0 0 0 0
0 0 0 0 0 0 0 0 0 x x x x x x
1 0 0 0 0 0 0 0 0 x x x x x x
0 0 0 0 0 0 0 0 0 x x x x x x
1 0 0 0 0 0 0 0 0 x x x x x x
0 0 0 0 0 0 0 0 0 x x x x x x
1 0 0 0 0 0 0 0 0 x x x x x x
0 0 0 0 0 0 0 0 0 x x x x x x
1 0 0 0 0 0 0 0 0 x x x x x x
0 0 0 0 0 0 0 0 0 x x x x x x
1 0 0 0 0 0 0 0 0 x x x x x x
0 0 0 0 0 0 0 0 0 x x x x x x
1 0 0 0 0 0 0 0 0 x x x x x x
0 0 0 0 0 0 0 0 0 x x x x x x
1 0 0 0 0 0 0 0 0 x x x x x x
0 0 0 0 0 0 0 0 0 x x x x x x
1 0 0 0 0 0 0 0 0 x x x x x x
0 0 0 0 0 0 0 0 0 x x x x x x
1 0 0 0 0 0 0 0 0 x x x x x x
0 0 0 0 0 0 0 0 0 x x x x x x
1 0 0 0 0 0 0 0 0 x x x x x x
0 0 0 0 0 0 0 0 0 x x x x x x
1 0 0 0 0 0 0 0 0 x x x x x x
0 0 0 0 0 0 0 0 0 x x x x x x
1 0 0 0 0 0 0 0 0 x x x x x x
0 0 0 0 0 0 0 0 0 x x x x x x
1 0 0 0 0 0 0 0 0 x x x x x x
0 0 0 0 0 0 0 0 0 x x x x x x
1 0 0 0 0 0 0 0 0 x x x x x x
0 0 0 0 0 0 0 0 0 x x x x x x
1 0 0 0 0 0 0 0 0 x x x x x x
0 0 0 0 0 0 0 0 0 x x x x x x
1 0 0 0 0 0 0 0 0 x x x x x x
0 0 0 0 0 0 0 0 0 x x x x x x
1 0 0 0 0 0 0 0 0 x x x x x x
0 0 0 0 0 0 0 0 0 x x x x x x
1 0 0 0 0 0 0 0 0 x x x x x x
0 0 0 0 0 0 0 0 0 x x x x x x
1 0 0 0 0 0 0 0 0 x x x x x x
0 0 0 0 0 0 0 0 0 x x x x x x
1 0 0 0 0 0 0 0 0 x x x x x x
0 0 0 0 0 0 0 0 0 5 0 0 0 0 0
1 0 0 0 0 0 0 0 0 5 0 0 0 0 0
0 0 0 0 0 0 0 1 0 5 0 0 0 0 0
1 0 0 0 0 0 0 1 0 5 0 0 0 0 0
0 0 0 0 0 0 0 0 0 x x x x x x
1 0 0 0 0 0 0 0 0 x x x x x x
0 0 0 0 0 0 0 0 0 x x x x x x
1 0 0 0 0 0 0 0 0 x x x x x x
0 0 0 0 0 0 0 0 0 x x x x x x
1 0 0 0 0 0 0 0 0 x x x x x x
0 0 0 0 0 0 0 0 0 x x x x x x
1 0 0 0 0 0 0 0 0 x x x x x x
0 0 0 0 0 0 0 0 0 x x x x x x
1 0 0 0 0 0 0 0 0 x x x x x x
0 0 0 0 0 0 0 0 0 x x x x x x
1 0 0 0 0 0 0 0 0 x x x x x x
0 0 0 0 0 0 0 0 0 x x x x x x
1 0 0 0 0 0 0 0 0 x x x x x x
0 0 0 0 0 0 0 0 0 x x x x x x
1 0 0 0 0 0 0 0 0 x x x x x x
0 0 0 0 0 0 0 0 0 x x x x x x
1 0 0 0 0 0 0 0 0 x x x x x x
0 0 0 0 0 0 0 0 0 x x x x x x
1 0 0 0 0 0 0 0 0 x x x x x x
0 0 0 0 0 0 0 0 0 x x x x x x
1 0 0 0 0 0 0 0 0 x x x x x x
0 0 0 0 0 0 0 0 0 x x x x x x
1 0 0 0 0 0 0 0 0 x x x x x x
0 0 0 0 0 0 0 0 0 x x x x x x
1 0 0 0 0 0 0 0 0 x x x x x x
0 0 0 0 0 0 0 0 0 x x x x x x
1 0 0 0 0 0 0 0 0 x x x x x x
0 0 0 0 0 0 0 0 0 x x x x x x
1 0 0 0 0 0 0 0 0 x x x x x x
0 0 0 0 0 0 0 0 0 x x x x x x
1 0 0 0 0 0 0 0 0 x x x x x x
0 0 0 0 0 0 0 0 0 x x x x x x
1 0 0 0 0 0 0 0 0 x x x x x x
0 0 0 0 0 0 0 0 0 x x x x x x
1 0 0 0 0 0 0 0 0 x x x x x x
0 0 0 0 0 0 0 0 0 x x x x x x
1 0 0 0 0 0 0 0 0 x x x x x x
0 0 0 0 0 0 0 0 0 x x x x x x
1 0 0 0 0 0 0 0 0 x x x x x x
0 0 0 0 0 0 0 0 0 0 0 0 1 0 0
1 0 0 0 0 0 0 0 0 0 0 0 1 0 0
0 0 0 1 0 0 0 0 0 0 0 0 1 0 0
1 0 0 1 0 0 0 0 0 0 0 0 1 0 0
0 0 0 0 0 0 0 0 0 x x x x x x
1 0 0 0 0 0 0 0 0 x x x x x x
0 0 0 0 0 0 0 0 0 x x x x x x
1 0 0 0 0 0 0 0 0 x x x x x x
0 0 0 0 0 0 0 0 0 x x x x x x
1 0 0 0 0 0 0 0 0 x x x x x x
0 0 0 0 0 0 0 0 0 x x x x x x
1 0 0 0 0 0 0 0 0 x x x x x x
0 0 0 0 0 0 0 0 0 x x x x x x
1 0 0 0 0 0 0 0 0 x x x x x x
0 0 0 0 0 0 0 0 0 x x x x x x
1 0 0 0 0 0 0 0 0 x x x x x x
0 0 0 0 0 0 0 0 0 x x x x x x
1 0 0 0 0 0 0 0 0 x x x x x x
0 0 0 0 0 0 0 0 0 x x x x x x
1 0 0 0 0 0 0 0 0 x x x x x x
0 0 0 0 0 0 0 0 0 x x x x x x
1 0 0 0 0 0 0 0 0 x x x x x x
0 0 0 0 0 0 0 0 0 x x x x x x
1 0 0 0 0 0 0 0 0 x x x x x x
0 0 0 0 0 0 0 0 0 x x x x x x
1 0 0 0 0 0 0 0 0 x x x x x x
0 0 0 0 0 0 0 0 0 x x x x x x
1 0 0 0 0 0 0 0 0 x x x x x x
0 0 0 0 0 0 0 0 0 x x x x x x
1 0 0 0 0 0 0 0 0 x x x x x x
0 0 0 0 0 0 0 0 0 x x x x x x
1 0 0 0 0 0 0 0 0 x x x x x x
0 0 0 0 0 0 0 0 0 x x x x x x
1 0 0 0 0 0 0 0 0 x x x x x x
0 0 0 0 0 0 0 0 0 x x x x x x
1 0 0 0 0 0 0 0 0 x x x x x x
0 0 0 0 0 0 0 0 0 x x x x x x
1 0 0 0 0 0 0 0 0 x x x x x x
0 0 0 0 0 0 0 0 0 x x x x x x
1 0 0 0 0 0 0 0 0 x x x x x x
0 0 0 0 0 0 0 0 0 x x x x x x
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*/

/* Test case TC4:
clock reset P5 P10 P20 Pcoffee Ptea Pchange Pnext Balance CoffeeOut TeaOut Change5 Change10 Change20
0 1 0 0 0 0 0 0 0 x x x x x x
1 1 0 0 0 0 0 0 0 0 0 0 0 0 0
0 0 0 0 1 0 0 0 0 0 0 0 0 0 0
1 0 0 0 1 0 0 0 0 0 0 0 0 0 0
0 0 0 0 0 0 0 0 0 x x x x x x
1 0 0 0 0 0 0 0 0 x x x x x x
0 0 0 0 0 0 0 0 0 x x x x x x
1 0 0 0 0 0 0 0 0 x x x x x x
0 0 0 0 0 0 0 0 0 x x x x x x
1 0 0 0 0 0 0 0 0 x x x x x x
0 0 0 0 0 0 0 0 0 x x x x x x
1 0 0 0 0 0 0 0 0 x x x x x x
0 0 0 0 0 0 0 0 0 x x x x x x
1 0 0 0 0 0 0 0 0 x x x x x x
0 0 0 0 0 0 0 0 0 x x x x x x
1 0 0 0 0 0 0 0 0 x x x x x x
0 0 0 0 0 0 0 0 0 x x x x x x
1 0 0 0 0 0 0 0 0 x x x x x x
0 0 0 0 0 0 0 0 0 x x x x x x
1 0 0 0 0 0 0 0 0 x x x x x x
0 0 0 0 0 0 0 0 0 x x x x x x
1 0 0 0 0 0 0 0 0 x x x x x x
0 0 0 0 0 0 0 0 0 x x x x x x
1 0 0 0 0 0 0 0 0 x x x x x x
0 0 0 0 0 0 0 0 0 x x x x x x
1 0 0 0 0 0 0 0 0 x x x x x x
0 0 0 0 0 0 0 0 0 x x x x x x
1 0 0 0 0 0 0 0 0 x x x x x x
0 0 0 0 0 0 0 0 0 x x x x x x
1 0 0 0 0 0 0 0 0 x x x x x x
0 0 0 0 0 0 0 0 0 x x x x x x
1 0 0 0 0 0 0 0 0 x x x x x x
0 0 0 0 0 0 0 0 0 x x x x x x
1 0 0 0 0 0 0 0 0 x x x x x x
0 0 0 0 0 0 0 0 0 x x x x x x
1 0 0 0 0 0 0 0 0 x x x x x x
0 0 0 0 0 0 0 0 0 x x x x x x
1 0 0 0 0 0 0 0 0 x x x x x x
0 0 0 0 0 0 0 0 0 x x x x x x
1 0 0 0 0 0 0 0 0 x x x x x x
0 0 0 0 0 0 0 0 0 x x x x x x
1 0 0 0 0 0 0 0 0 x x x x x x
0 0 0 0 0 0 0 0 0 x x x x x x
1 0 0 0 0 0 0 0 0 x x x x x x
0 0 0 0 0 0 0 0 0 20 0 0 0 0 0
1 0 0 0 0 0 0 0 0 20 0 0 0 0 0
0 0 0 0 1 0 0 0 0 20 0 0 0 0 0
1 0 0 0 1 0 0 0 0 20 0 0 0 0 0
0 0 0 0 0 0 0 0 0 x x x x x x
1 0 0 0 0 0 0 0 0 x x x x x x
0 0 0 0 0 0 0 0 0 x x x x x x
1 0 0 0 0 0 0 0 0 x x x x x x
0 0 0 0 0 0 0 0 0 x x x x x x
1 0 0 0 0 0 0 0 0 x x x x x x
0 0 0 0 0 0 0 0 0 x x x x x x
1 0 0 0 0 0 0 0 0 x x x x x x
0 0 0 0 0 0 0 0 0 x x x x x x
1 0 0 0 0 0 0 0 0 x x x x x x
0 0 0 0 0 0 0 0 0 x x x x x x
1 0 0 0 0 0 0 0 0 x x x x x x
0 0 0 0 0 0 0 0 0 x x x x x x
1 0 0 0 0 0 0 0 0 x x x x x x
0 0 0 0 0 0 0 0 0 x x x x x x
1 0 0 0 0 0 0 0 0 x x x x x x
0 0 0 0 0 0 0 0 0 x x x x x x
1 0 0 0 0 0 0 0 0 x x x x x x
0 0 0 0 0 0 0 0 0 x x x x x x
1 0 0 0 0 0 0 0 0 x x x x x x
0 0 0 0 0 0 0 0 0 x x x x x x
1 0 0 0 0 0 0 0 0 x x x x x x
0 0 0 0 0 0 0 0 0 x x x x x x
1 0 0 0 0 0 0 0 0 x x x x x x
0 0 0 0 0 0 0 0 0 x x x x x x
1 0 0 0 0 0 0 0 0 x x x x x x
0 0 0 0 0 0 0 0 0 x x x x x x
1 0 0 0 0 0 0 0 0 x x x x x x
0 0 0 0 0 0 0 0 0 x x x x x x
1 0 0 0 0 0 0 0 0 x x x x x x
0 0 0 0 0 0 0 0 0 x x x x x x
1 0 0 0 0 0 0 0 0 x x x x x x
0 0 0 0 0 0 0 0 0 x x x x x x
1 0 0 0 0 0 0 0 0 x x x x x x
0 0 0 0 0 0 0 0 0 x x x x x x
1 0 0 0 0 0 0 0 0 x x x x x x
0 0 0 0 0 0 0 0 0 x x x x x x
1 0 0 0 0 0 0 0 0 x x x x x x
0 0 0 0 0 0 0 0 0 x x x x x x
1 0 0 0 0 0 0 0 0 x x x x x x
0 0 0 0 0 0 0 0 0 40 0 0 0 0 0
1 0 0 0 0 0 0 0 0 40 0 0 0 0 0
0 0 0 0 0 0 1 0 0 40 0 0 0 0 0
1 0 0 0 0 0 1 0 0 40 0 0 0 0 0
0 0 0 0 0 0 0 0 0 x x x x x x
1 0 0 0 0 0 0 0 0 x x x x x x
0 0 0 0 0 0 0 0 0 x x x x x x
1 0 0 0 0 0 0 0 0 x x x x x x
0 0 0 0 0 0 0 0 0 x x x x x x
1 0 0 0 0 0 0 0 0 x x x x x x
0 0 0 0 0 0 0 0 0 x x x x x x
1 0 0 0 0 0 0 0 0 x x x x x x
0 0 0 0 0 0 0 0 0 x x x x x x
1 0 0 0 0 0 0 0 0 x x x x x x
0 0 0 0 0 0 0 0 0 x x x x x x
1 0 0 0 0 0 0 0 0 x x x x x x
0 0 0 0 0 0 0 0 0 x x x x x x
1 0 0 0 0 0 0 0 0 x x x x x x
0 0 0 0 0 0 0 0 0 x x x x x x
1 0 0 0 0 0 0 0 0 x x x x x x
0 0 0 0 0 0 0 0 0 x x x x x x
1 0 0 0 0 0 0 0 0 x x x x x x
0 0 0 0 0 0 0 0 0 x x x x x x
1 0 0 0 0 0 0 0 0 x x x x x x
0 0 0 0 0 0 0 0 0 x x x x x x
1 0 0 0 0 0 0 0 0 x x x x x x
0 0 0 0 0 0 0 0 0 x x x x x x
1 0 0 0 0 0 0 0 0 x x x x x x
0 0 0 0 0 0 0 0 0 x x x x x x
1 0 0 0 0 0 0 0 0 x x x x x x
0 0 0 0 0 0 0 0 0 x x x x x x
1 0 0 0 0 0 0 0 0 x x x x x x
0 0 0 0 0 0 0 0 0 x x x x x x
1 0 0 0 0 0 0 0 0 x x x x x x
0 0 0 0 0 0 0 0 0 x x x x x x
1 0 0 0 0 0 0 0 0 x x x x x x
0 0 0 0 0 0 0 0 0 x x x x x x
1 0 0 0 0 0 0 0 0 x x x x x x
0 0 0 0 0 0 0 0 0 x x x x x x
1 0 0 0 0 0 0 0 0 x x x x x x
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*/
