// Digital circuit vendingmachine.dig as structural Verilog
module vendingmachine (
  input  reset,
  input  P5,
  input  P10,
  input  P20,
  input  Pcoffee,
  input  Ptea,
  input  Pchange,
  input  Pnext,
  input  clock,
  output Q0,
  output Q1,
  output Q2,
  output Q3,
  output [5:0] Balance,
  output CoffeeOut,
  output TeaOut,
  output [1:0] Change5,
  output [1:0] Change10,
  output [1:0] Change20
);

  wire AddChange5, AddChange10, AddChange20, and_1_out, and_2_out, and_3_out, and_4_out, and_5_out,
       and_6_out, and_7_out, and_8_out, and_9_out, and_10_out, and_11_out, and_12_out, and_13_out,
       and_14_out, and_15_out, and_16_out, and_17_out, and_18_out, and_19_out, and_20_out, and_21_out,
       and_22_out, and_23_out, and_24_out, Balance_gt__eq_5, Balance_gt__eq_10, Balance_gt__eq_20,
       Balance_gt__eq_25, Balance_lt__eq_30, Balance_lt__eq_40, Balance_lt__eq_45, canAdd5, canAdd10,
       canAdd20, canPayCoffee, canPayTea, ChangePrep, clearBalance, driverinvsel_1_out, driverinvsel_2_out,
       driverinvsel_3_out, driverinvsel_4_out, Idle, loadCoffeeOut, loadTeaOut, multiplexer_1_out,
       multiplexer_2_out, multiplexer_3_out, multiplexer_4_out, NextOrder, not_1_out, not_2_out, or_1_out,
       or_2_out, or_3_out, or_4_out, or_5_out, or_6_out, or_7_out, or_8_out, or_9_out, or_10_out, or_11_out,
       or_12_out, or_13_out, or_14_out, or_15_out, or_16_out, or_17_out, or_18_out, or_19_out, P5_t, P10_t,
       P20_t, Pchange_t, Pcoffee_t, Pnext_t, Ptea_t, S1_n_2_q, S1_n_3_q, S1_n_4_q, S1_n_5_q, S1_n_6_q,
       S1_n_7_q, S1_n_q;
  wire [5:0] Balance_q, multiplexer_5_out;
  wire [6:0] multiplexer_6_out;
  wire [6:6] add_1_s;

  and and_1 (and_1_out, P5, P5_t);
  and and_2 (and_2_out, P5, S1_n_q);
  and and_3 (and_3_out, ~S1_n_q, P5, ~P5_t);  // And
  and and_4 (and_4_out, Ptea, Ptea_t);
  and and_5 (and_5_out, Ptea, S1_n_2_q);
  and and_6 (and_6_out, ~S1_n_2_q, Ptea, ~Ptea_t);  // And
  or or_1 (or_1_out, and_1_out, and_2_out);
  D_FF S0_n (.D(and_3_out), .C(clock), .Q(P5_t));  // open: nQ
  or or_2 (or_2_out, and_4_out, and_5_out);
  D_FF S0_n_2 (.D(and_6_out), .C(clock), .Q(Ptea_t));  // open: nQ
  D_FF S1_n (.D(or_1_out), .C(clock), .Q(S1_n_q));  // open: nQ
  D_FF S1_n_2 (.D(or_2_out), .C(clock), .Q(S1_n_2_q));  // open: nQ
  and and_7 (and_7_out, P10, P10_t);
  and and_8 (and_8_out, P10, S1_n_3_q);
  and and_9 (and_9_out, ~S1_n_3_q, P10, ~P10_t);  // And
  and and_10 (and_10_out, Pchange, Pchange_t);
  and and_11 (and_11_out, Pchange, S1_n_4_q);
  and and_12 (and_12_out, ~S1_n_4_q, Pchange, ~Pchange_t);  // And
  or or_3 (or_3_out, and_7_out, and_8_out);
  D_FF S0_n_3 (.D(and_9_out), .C(clock), .Q(P10_t));  // open: nQ
  or or_4 (or_4_out, and_10_out, and_11_out);
  D_FF S0_n_4 (.D(and_12_out), .C(clock), .Q(Pchange_t));  // open: nQ
  D_FF S1_n_3 (.D(or_3_out), .C(clock), .Q(S1_n_3_q));  // open: nQ
  D_FF S1_n_4 (.D(or_4_out), .C(clock), .Q(S1_n_4_q));  // open: nQ
  and and_13 (and_13_out, Pnext, Pnext_t);
  and and_14 (and_14_out, Pnext, S1_n_6_q);
  and and_15 (and_15_out, ~S1_n_6_q, Pnext, ~Pnext_t);  // And
  and and_16 (and_16_out, P20, P20_t);
  and and_17 (and_17_out, P20, S1_n_5_q);
  and and_18 (and_18_out, ~S1_n_5_q, P20, ~P20_t);  // And
  or or_5 (or_5_out, and_16_out, and_17_out);
  D_FF S0_n_5 (.D(and_18_out), .C(clock), .Q(P20_t));  // open: nQ
  or or_6 (or_6_out, and_13_out, and_14_out);
  D_FF S0_n_6 (.D(and_15_out), .C(clock), .Q(Pnext_t));  // open: nQ
  D_FF S1_n_5 (.D(or_5_out), .C(clock), .Q(S1_n_5_q));  // open: nQ
  D_FF S1_n_6 (.D(or_6_out), .C(clock), .Q(S1_n_6_q));  // open: nQ
  and and_19 (and_19_out, Pcoffee, Pcoffee_t);
  and and_20 (and_20_out, Pcoffee, S1_n_7_q);
  and and_21 (and_21_out, ~S1_n_7_q, Pcoffee, ~Pcoffee_t);  // And
  or or_7 (or_7_out, and_19_out, and_20_out);
  D_FF S0_n_7 (.D(and_21_out), .C(clock), .Q(Pcoffee_t));  // open: nQ
  D_FF S1_n_7 (.D(or_7_out), .C(clock), .Q(S1_n_7_q));  // open: nQ
  and and_22 (and_22_out, ~Balance_gt__eq_20, Balance_gt__eq_10);  // And
  and and_23 (and_23_out, ~Balance_gt__eq_20, Balance_gt__eq_10);  // And
  or or_8 (or_8_out, Balance_gt__eq_5, reset);
  and and_24 (and_24_out, ~Balance_gt__eq_10, Balance_gt__eq_5);  // And
  or or_9 (or_9_out, canAdd5, canAdd20, canPayCoffee, reset);
  and and_25 (canAdd20, P20_t, Balance_lt__eq_30);
  and and_26 (canAdd10, P10_t, Balance_lt__eq_40);
  and and_27 (canAdd5, P5_t, Balance_lt__eq_45);
  and and_28 (canPayTea, Ptea_t, Balance_gt__eq_20);
  and and_29 (canPayCoffee, Pcoffee_t, Balance_gt__eq_25);
  or or_10 (or_10_out, Pchange_t, reset);
  or or_11 (or_11_out, Pchange_t, reset);
  or or_12 (or_12_out, canPayCoffee, canPayTea, reset);
  or or_13 (or_13_out, and_24_out, reset);
  or or_14 (or_14_out, canAdd20, canAdd10, reset);
  or or_15 (or_15_out, Balance_gt__eq_20, and_22_out, reset);
  or or_16 (or_16_out, Pnext_t, reset);
  or or_17 (or_17_out, and_23_out, reset);
  not not_1 (not_1_out, Pchange_t);
  not not_2 (not_2_out, Pchange_t);
  Multiplexer #(.Selector_Bits(4)) multiplexer_1 (
    .sel({Q3, Q2, Q1, Q0}), .in_0(or_10_out), .in_1(1'b0), .in_2(1'b0), .in_3(1'b0), .in_4(1'b0),
    .in_5(1'b0), .in_6(or_11_out), .in_7(1'b0), .in_8(1'b1), .in_9(or_8_out), .in_10(1'b1), .in_11(1'b1),
    .in_12(1'b1), .in_13(1'b0), .in_14(1'b0), .in_15(1'b0), .out(multiplexer_1_out));
  Multiplexer #(.Selector_Bits(4)) multiplexer_2 (
    .sel({Q3, Q2, Q1, Q0}), .in_0(or_12_out), .in_1(1'b0), .in_2(1'b0), .in_3(1'b0), .in_4(1'b1),
    .in_5(1'b1), .in_6(not_1_out), .in_7(1'b0), .in_8(1'b0), .in_9(or_13_out), .in_10(1'b0), .in_11(1'b0),
    .in_12(1'b0), .in_13(1'b0), .in_14(1'b0), .in_15(1'b0), .out(multiplexer_2_out));
  Multiplexer #(.Selector_Bits(4)) multiplexer_3 (
    .sel({Q3, Q2, Q1, Q0}), .in_0(or_14_out), .in_1(1'b0), .in_2(1'b0), .in_3(1'b0), .in_4(1'b1),
    .in_5(1'b1), .in_6(not_2_out), .in_7(1'b0), .in_8(1'b0), .in_9(or_15_out), .in_10(1'b0), .in_11(1'b0),
    .in_12(1'b0), .in_13(1'b0), .in_14(1'b0), .in_15(1'b0), .out(multiplexer_3_out));
  Multiplexer #(.Selector_Bits(4)) multiplexer_4 (
    .sel({Q3, Q2, Q1, Q0}), .in_0(or_9_out), .in_1(1'b0), .in_2(1'b0), .in_3(1'b0), .in_4(1'b0), .in_5(1'b0),
    .in_6(or_16_out), .in_7(1'b0), .in_8(1'b1), .in_9(or_17_out), .in_10(1'b1), .in_11(1'b1), .in_12(1'b1),
    .in_13(1'b0), .in_14(1'b0), .in_15(1'b0), .out(multiplexer_4_out));
  D_FF u_Q3 (.D(multiplexer_1_out), .C(clock), .Q(Q3));  // open: nQ
  D_FF u_Q2 (.D(multiplexer_2_out), .C(clock), .Q(Q2));  // open: nQ
  D_FF u_Q1 (.D(multiplexer_3_out), .C(clock), .Q(Q1));  // open: nQ
  D_FF u_Q0 (.D(multiplexer_4_out), .C(clock), .Q(Q0));  // open: nQ
  Demultiplexer #(.Selector_Bits(4)) demultiplexer_1 (
    .sel({Q3, Q2, Q1, Q0}), .in(1'b1), .out_0(Idle), .out_4(loadTeaOut), .out_5(loadCoffeeOut),
    .out_7(NextOrder), .out_8(ChangePrep), .out_10(AddChange20), .out_11(AddChange10), .out_12(AddChange5),
    .out_15(clearBalance));  // open: out_1, out_2, out_3, out_6, out_9, out_13, out_14
  Multiplexer #(.Bits(6)) multiplexer_5 (.sel(clearBalance), .in_0(Balance), .in_1({6{1'b0}}), .out(multiplexer_5_out));
  Register #(.Bits(6)) u_Balance (.D(multiplexer_5_out), .C(clock), .en(1'b1), .Q(Balance_q));
  Comparator #(.Bits(6)) Balance_lt_46 (.a(Balance), .b(6'b101110), .lt(Balance_lt__eq_45));  // open: gt, eq
  Comparator #(.Bits(6)) Balance_lt_41 (.a(Balance), .b(6'b101001), .lt(Balance_lt__eq_40));  // open: gt, eq
  Comparator #(.Bits(6)) Balance_lt_31 (.a(Balance), .b(6'b011111), .lt(Balance_lt__eq_30));  // open: gt, eq
  Comparator #(.Bits(6)) Balance_gt_19 (.a(Balance), .b(6'b010011), .gt(Balance_gt__eq_20));  // open: eq, lt
  Comparator #(.Bits(6)) Balance_gt_24 (.a(Balance), .b(6'b011000), .gt(Balance_gt__eq_25));  // open: eq, lt
  Comparator #(.Bits(6)) Balance_gt_9 (.a(Balance), .b(6'b001001), .gt(Balance_gt__eq_10));  // open: eq, lt
  Comparator #(.Bits(6)) Balance_gt_4 (.a(Balance), .b(6'b000100), .gt(Balance_gt__eq_5));  // open: eq, lt
  Multiplexer #(.Selector_Bits(4), .Bits(7)) multiplexer_6 (
    .sel({Q3, Q2, Q1, Q0}), .in_0({7{1'b0}}), .in_1(7'b0000101), .in_2(7'b0001010), .in_3(7'b0010100),
    .in_4(7'b1101100), .in_5(7'b1100111), .in_6({7{1'b0}}), .in_7({7{1'b0}}), .in_8({7{1'b0}}),
    .in_9({7{1'b0}}), .in_10(7'b1101100), .in_11(7'b1110110), .in_12(7'b1111011), .in_13({7{1'b0}}),
    .in_14({7{1'b0}}), .in_15({7{1'b0}}), .out(multiplexer_6_out));
  Add #(.Bits(7)) add_1 (
    .a({1'b0, Balance_q}), .b(multiplexer_6_out), .c_i(1'b0), .s({add_1_s[6], Balance}));  // open: c_o
  or or_18 (or_18_out, clearBalance, ChangePrep, NextOrder, Idle);
  or or_19 (or_19_out, clearBalance, ChangePrep);
  assign driverinvsel_1_out = ~loadCoffeeOut ? CoffeeOut : 1'bz;  // DriverInvSel driverinvsel_1
  assign driverinvsel_1_out = loadCoffeeOut ? 1'b1 : 1'bz;  // Driver driver_1
  assign driverinvsel_2_out = ~loadTeaOut ? TeaOut : 1'bz;  // DriverInvSel driverinvsel_2
  assign driverinvsel_2_out = loadTeaOut ? 1'b1 : 1'bz;  // Driver driver_2
  Counter #(.Bits(2)) counter_1 (.en(AddChange20), .C(clock), .clr(or_19_out), .out(Change20));  // open: ovf
  Counter #(.Bits(2)) counter_2 (.en(AddChange10), .C(clock), .clr(or_19_out), .out(Change10));  // open: ovf
  Counter #(.Bits(2)) counter_3 (.en(AddChange5), .C(clock), .clr(or_19_out), .out(Change5));  // open: ovf
  assign driverinvsel_3_out = ~or_18_out ? driverinvsel_1_out : 1'bz;  // DriverInvSel driverinvsel_3
  assign driverinvsel_3_out = or_18_out ? 1'b0 : 1'bz;  // Driver driver_3
  assign driverinvsel_4_out = ~or_18_out ? driverinvsel_2_out : 1'bz;  // DriverInvSel driverinvsel_4
  assign driverinvsel_4_out = or_18_out ? 1'b0 : 1'bz;  // Driver driver_4
  Register u_CoffeeOut (.D(driverinvsel_3_out), .C(clock), .en(1'b1), .Q(CoffeeOut));
  Register u_TeaOut (.D(driverinvsel_4_out), .C(clock), .en(1'b1), .Q(TeaOut));

  // Other names for the same wires on the sheet: clearChange5 = clearBalance; clearChange10 = clearBalance;
  //   clearChange20 = clearBalance; Reset_t = clearBalance; State[3:0] = {Q3, Q2, Q1, Q0}
endmodule

/* Test case TC1:
clock reset P5 P10 P20 Pcoffee Ptea Pchange Pnext Balance CoffeeOut TeaOut Change5 Change10 Change20
0 1 0 0 0 0 0 0 0 x x x x x x
1 1 0 0 0 0 0 0 0 0 0 0 0 0 0
0 0 1 0 0 0 0 0 0 0 0 0 0 0 0
1 0 1 0 0 0 0 0 0 0 0 0 0 0 0
0 0 0 0 0 0 0 0 0 x x x x x x
1 0 0 0 0 0 0 0 0 x x x x x x
0 0 0 0 0 0 0 0 0 x x x x x x
1 0 0 0 0 0 0 0 0 x x x x x x
0 0 0 0 0 0 0 0 0 x x x x x x
1 0 0 0 0 0 0 0 0 x x x x x x
0 0 0 0 0 0 0 0 0 x x x x x x
1 0 0 0 0 0 0 0 0 x x x x x x
0 0 0 0 0 0 0 0 0 x x x x x x
1 0 0 0 0 0 0 0 0 x x x x x x
0 0 0 0 0 0 0 0 0 x x x x x x
1 0 0 0 0 0 0 0 0 x x x x x x
0 0 0 0 0 0 0 0 0 x x x x x x
1 0 0 0 0 0 0 0 0 x x x x x x
0 0 0 0 0 0 0 0 0 x x x x x x
1 0 0 0 0 0 0 0 0 x x x x x x
0 0 0 0 0 0 0 0 0 x x x x x x
1 0 0 0 0 0 0 0 0 x x x x x x
0 0 0 0 0 0 0 0 0 x x x x x x
1 0 0 0 0 0 0 0 0 x x x x x x
0 0 0 0 0 0 0 0 0 x x x x x x
1 0 0 0 0 0 0 0 0 x x x x x x
0 0 0 0 0 0 0 0 0 x x x x x x
1 0 0 0 0 0 0 0 0 x x x x x x
0 0 0 0 0 0 0 0 0 x x x x x x
1 0 0 0 0 0 0 0 0 x x x x x x
0 0 0 0 0 0 0 0 0 x x x x x x
1 0 0 0 0 0 0 0 0 x x x x x x
0 0 0 0 0 0 0 0 0 x x x x x x
1 0 0 0 0 0 0 0 0 x x x x x x
0 0 0 0 0 0 0 0 0 x x x x x x
1 0 0 0 0 0 0 0 0 x x x x x x
0 0 0 0 0 0 0 0 0 x x x x x x
1 0 0 0 0 0 0 0 0 x x x x x x
0 0 0 0 0 0 0 0 0 x x x x x x
1 0 0 0 0 0 0 0 0 x x x x x x
0 0 0 0 0 0 0 0 0 x x x x x x
1 0 0 0 0 0 0 0 0 x x x x x x
0 0 0 0 0 0 0 0 0 x x x x x x
1 0 0 0 0 0 0 0 0 x x x x x x
0 0 0 0 0 0 0 0 0 5 0 0 0 0 0
1 0 0 0 0 0 0 0 0 5 0 0 0 0 0
0 0 0 1 0 0 0 0 0 5 0 0 0 0 0
1 0 0 1 0 0 0 0 0 5 0 0 0 0 0
0 0 0 0 0 0 0 0 0 x x x x x x
1 0 0 0 0 0 0 0 0 x x x x x x
0 0 0 0 0 0 0 0 0 x x x x x x
1 0 0 0 0 0 0 0 0 x x x x x x
0 0 0 0 0 0 0 0 0 x x x x x x
1 0 0 0 0 0 0 0 0 x x x x x x
0 0 0 0 0 0 0 0 0 x x x x x x
1 0 0 0 0 0 0 0 0 x x x x x x
0 0 0 0 0 0 0 0 0 x x x x x x
1 0 0 0 0 0 0 0 0 x x x x x x
0 0 0 0 0 0 0 0 0 x x x x x x
1 0 0 0 0 0 0 0 0 x x x x x x
0 0 0 0 0 0 0 0 0 x x x x x x
1 0 0 0 0 0 0 0 0 x x x x x x
0 0 0 0 0 0 0 0 0 x x x x x x
1 0 0 0 0 0 0 0 0 x x x x x x
0 0 0 0 0 0 0 0 0 x x x x x x
1 0 0 0 0 0 0 0 0 x x x x x x
0 0 0 0 0 0 0 0 0 x x x x x x
1 0 0 0 0 0 0 0 0 x x x x x x
0 0 0 0 0 0 0 0 0 x x x x x x
1 0 0 0 0 0 0 0 0 x x x x x x
0 0 0 0 0 0 0 0 0 x x x x x x
1 0 0 0 0 0 0 0 0 x x x x x x
0 0 0 0 0 0 0 0 0 x x x x x x
1 0 0 0 0 0 0 0 0 x x x x x x
0 0 0 0 0 0 0 0 0 x x x x x x
1 0 0 0 0 0 0 0 0 x x x x x x
0 0 0 0 0 0 0 0 0 x x x x x x
1 0 0 0 0 0 0 0 0 x x x x x x
0 0 0 0 0 0 0 0 0 x x x x x x
1 0 0 0 0 0 0 0 0 x x x x x x
0 0 0 0 0 0 0 0 0 x x x x x x
1 0 0 0 0 0 0 0 0 x x x x x x
0 0 0 0 0 0 0 0 0 x x x x x x
1 0 0 0 0 0 0 0 0 x x x x x x
0 0 0 0 0 0 0 0 0 x x x x x x
1 0 0 0 0 0 0 0 0 x x x x x x
0 0 0 0 0 0 0 0 0 x x x x x x
1 0 0 0 0 0 0 0 0 x x x x x x
0 0 0 0 0 0 0 0 0 15 0 0 0 0 0
1 0 0 0 0 0 0 0 0 15 0 0 0 0 0
0 0 0 0 1 0 0 0 0 15 0 0 0 0 0
1 0 0 0 1 0 0 0 0 15 0 0 0 0 0
0 0 0 0 0 0 0 0 0 x x x x x x
1 0 0 0 0 0 0 0 0 x x x x x x
0 0 0 0 0 0 0 0 0 x x x x x x
1 0 0 0 0 0 0 0 0 x x x x x x
0 0 0 0 0 0 0 0 0 x x x x x x
1 0 0 0 0 0 0 0 0 x x x x x x
0 0 0 0 0 0 0 0 0 x x x x x x
1 0 0 0 0 0 0 0 0 x x x x x x
0 0 0 0 0 0 0 0 0 x x x x x x
1 0 0 0 0 0 0 0 0 x x x x x x
0 0 0 0 0 0 0 0 0 x x x x x x
1 0 0 0 0 0 0 0 0 x x x x x x
0 0 0 0 0 0 0 0 0 x x x x x x
1 0 0 0 0 0 0 0 0 x x x x x x
0 0 0 0 0 0 0 0 0 x x x x x x
1 0 0 0 0 0 0 0 0 x x x x x x
0 0 0 0 0 0 0 0 0 x x x x x x
1 0 0 0 0 0 0 0 0 x x x x x x
0 0 0 0 0 0 0 0 0 x x x x x x
1 0 0 0 0 0 0 0 0 x x x x x x
0 0 0 0 0 0 0 0 0 x x x x x x
1 0 0 0 0 0 0 0 0 x x x x x x
0 0 0 0 0 0 0 0 0 x x x x x x
1 0 0 0 0 0 0 0 0 x x x x x x
0 0 0 0 0 0 0 0 0 x x x x x x
1 0 0 0 0 0 0 0 0 x x x x x x
0 0 0 0 0 0 0 0 0 x x x x x x
1 0 0 0 0 0 0 0 0 x x x x x x
0 0 0 0 0 0 0 0 0 x x x x x x
1 0 0 0 0 0 0 0 0 x x x x x x
0 0 0 0 0 0 0 0 0 x x x x x x
1 0 0 0 0 0 0 0 0 x x x x x x
0 0 0 0 0 0 0 0 0 x x x x x x
1 0 0 0 0 0 0 0 0 x x x x x x
0 0 0 0 0 0 0 0 0 x x x x x x
1 0 0 0 0 0 0 0 0 x x x x x x
0 0 0 0 0 0 0 0 0 x x x x x x
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*/

/* Test case TC2:
clock reset P5 P10 P20 Pcoffee Ptea Pchange Pnext Balance CoffeeOut TeaOut Change5 Change10 Change20
0 1 0 0 0 0 0 0 0 x x x x x x
1 1 0 0 0 0 0 0 0 0 0 0 0 0 0
0 0 0 0 0 1 0 0 0 0 0 0 0 0 0
1 0 0 0 0 1 0 0 0 0 0 0 0 0 0
0 0 0 0 0 0 0 0 0 x x x x x x
1 0 0 0 0 0 0 0 0 x x x x x x
0 0 0 0 0 0 0 0 0 x x x x x x
1 0 0 0 0 0 0 0 0 x x x x x x
0 0 0 0 0 0 0 0 0 x x x x x x
1 0 0 0 0 0 0 0 0 x x x x x x
0 0 0 0 0 0 0 0 0 x x x x x x
1 0 0 0 0 0 0 0 0 x x x x x x
0 0 0 0 0 0 0 0 0 x x x x x x
1 0 0 0 0 0 0 0 0 x x x x x x
0 0 0 0 0 0 0 0 0 x x x x x x
1 0 0 0 0 0 0 0 0 x x x x x x
0 0 0 0 0 0 0 0 0 x x x x x x
1 0 0 0 0 0 0 0 0 x x x x x x
0 0 0 0 0 0 0 0 0 x x x x x x
1 0 0 0 0 0 0 0 0 x x x x x x
0 0 0 0 0 0 0 0 0 x x x x x x
1 0 0 0 0 0 0 0 0 x x x x x x
0 0 0 0 0 0 0 0 0 x x x x x x
1 0 0 0 0 0 0 0 0 x x x x x x
0 0 0 0 0 0 0 0 0 x x x x x x
1 0 0 0 0 0 0 0 0 x x x x x x
0 0 0 0 0 0 0 0 0 x x x x x x
1 0 0 0 0 0 0 0 0 x x x x x x
0 0 0 0 0 0 0 0 0 x x x x x x
1 0 0 0 0 0 0 0 0 x x x x x x
0 0 0 0 0 0 0 0 0 x x x x x x
1 0 0 0 0 0 0 0 0 x x x x x x
0 0 0 0 0 0 0 0 0 x x x x x x
1 0 0 0 0 0 0 0 0 x x x x x x
0 0 0 0 0 0 0 0 0 x x x x x x
1 0 0 0 0 0 0 0 0 x x x x x x
0 0 0 0 0 0 0 0 0 x x x x x x
1 0 0 0 0 0 0 0 0 x x x x x x
0 0 0 0 0 0 0 0 0 x x x x x x
1 0 0 0 0 0 0 0 0 x x x x x x
0 0 0 0 0 0 0 0 0 x x x x x x
1 0 0 0 0 0 0 0 0 x x x x x x
0 0 0 0 0 0 0 0 0 x x x x x x
1 0 0 0 0 0 0 0 0 x x x x x x
0 0 0 0 0 0 0 0 0 0 0 0 0 0 0
1 0 0 0 0 0 0 0 0 0 0 0 0 0 0
0 0 0 0 0 0 1 0 0 0 0 0 0 0 0
1 0 0 0 0 0 1 0 0 0 0 0 0 0 0
0 0 0 0 0 0 0 0 0 x x x x x x
1 0 0 0 0 0 0 0 0 x x x x x x
0 0 0 0 0 0 0 0 0 x x x x x x
1 0 0 0 0 0 0 0 0 x x x x x x
0 0 0 0 0 0 0 0 0 x x x x x x
1 0 0 0 0 0 0 0 0 x x x x x x
0 0 0 0 0 0 0 0 0 x x x x x x
1 0 0 0 0 0 0 0 0 x x x x x x
0 0 0 0 0 0 0 0 0 x x x x x x
1 0 0 0 0 0 0 0 0 x x x x x x
0 0 0 0 0 0 0 0 0 x x x x x x
1 0 0 0 0 0 0 0 0 x x x x x x
0 0 0 0 0 0 0 0 0 x x x x x x
1 0 0 0 0 0 0 0 0 x x x x x x
0 0 0 0 0 0 0 0 0 x x x x x x
1 0 0 0 0 0 0 0 0 x x x x x x
0 0 0 0 0 0 0 0 0 x x x x x x
1 0 0 0 0 0 0 0 0 x x x x x x
0 0 0 0 0 0 0 0 0 x x x x x x
1 0 0 0 0 0 0 0 0 x x x x x x
0 0 0 0 0 0 0 0 0 x x x x x x
1 0 0 0 0 0 0 0 0 x x x x x x
0 0 0 0 0 0 0 0 0 x x x x x x
1 0 0 0 0 0 0 0 0 x x x x x x
0 0 0 0 0 0 0 0 0 x x x x x x
1 0 0 0 0 0 0 0 0 x x x x x x
0 0 0 0 0 0 0 0 0 x x x x x x
1 0 0 0 0 0 0 0 0 x x x x x x
0 0 0 0 0 0 0 0 0 x x x x x x
1 0 0 0 0 0 0 0 0 x x x x x x
0 0 0 0 0 0 0 0 0 x x x x x x
1 0 0 0 0 0 0 0 0 x x x x x x
0 0 0 0 0 0 0 0 0 x x x x x x
1 0 0 0 0 0 0 0 0 x x x x x x
0 0 0 0 0 0 0 0 0 x x x x x x
1 0 0 0 0 0 0 0 0 x x x x x x
0 0 0 0 0 0 0 0 0 x x x x x x
1 0 0 0 0 0 0 0 0 x x x x x x
0 0 0 0 0 0 0 0 0 x x x x x x
1 0 0 0 0 0 0 0 0 x x x x x x
0 0 0 0 0 0 0 0 0 0 0 0 0 0 0
1 0 0 0 0 0 0 0 0 0 0 0 0 0 0
0 0 0 0 1 0 0 0 0 0 0 0 0 0 0
1 0 0 0 1 0 0 0 0 0 0 0 0 0 0
0 0 0 0 0 0 0 0 0 x x x x x x
1 0 0 0 0 0 0 0 0 x x x x x x
0 0 0 0 0 0 0 0 0 x x x x x x
1 0 0 0 0 0 0 0 0 x x x x x x
0 0 0 0 0 0 0 0 0 x x x x x x
1 0 0 0 0 0 0 0 0 x x x x x x
0 0 0 0 0 0 0 0 0 x x x x x x
1 0 0 0 0 0 0 0 0 x x x x x x
0 0 0 0 0 0 0 0 0 x x x x x x
1 0 0 0 0 0 0 0 0 x x x x x x
0 0 0 0 0 0 0 0 0 x x x x x x
1 0 0 0 0 0 0 0 0 x x x x x x
0 0 0 0 0 0 0 0 0 x x x x x x
1 0 0 0 0 0 0 0 0 x x x x x x
0 0 0 0 0 0 0 0 0 x x x x x x
1 0 0 0 0 0 0 0 0 x x x x x x
0 0 0 0 0 0 0 0 0 x x x x x x
1 0 0 0 0 0 0 0 0 x x x x x x
0 0 0 0 0 0 0 0 0 x x x x x x
1 0 0 0 0 0 0 0 0 x x x x x x
0 0 0 0 0 0 0 0 0 x x x x x x
1 0 0 0 0 0 0 0 0 x x x x x x
0 0 0 0 0 0 0 0 0 x x x x x x
1 0 0 0 0 0 0 0 0 x x x x x x
0 0 0 0 0 0 0 0 0 x x x x x x
1 0 0 0 0 0 0 0 0 x x x x x x
0 0 0 0 0 0 0 0 0 x x x x x x
1 0 0 0 0 0 0 0 0 x x x x x x
0 0 0 0 0 0 0 0 0 x x x x x x
1 0 0 0 0 0 0 0 0 x x x x x x
0 0 0 0 0 0 0 0 0 x x x x x x
1 0 0 0 0 0 0 0 0 x x x x x x
0 0 0 0 0 0 0 0 0 x x x x x x
1 0 0 0 0 0 0 0 0 x x x x x x
0 0 0 0 0 0 0 0 0 x x x x x x
1 0 0 0 0 0 0 0 0 x x x x x x
0 0 0 0 0 0 0 0 0 x x x x x x
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*/

/* Test case TC3:
clock reset P5 P10 P20 Pcoffee Ptea Pchange Pnext Balance CoffeeOut TeaOut Change5 Change10 Change20
0 1 0 0 0 0 0 0 0 x x x x x x
1 1 0 0 0 0 0 0 0 0 0 0 0 0 0
0 0 1 0 0 0 0 0 0 0 0 0 0 0 0
1 0 1 0 0 0 0 0 0 0 0 0 0 0 0
0 0 0 0 0 0 0 0 0 x x x x x x
1 0 0 0 0 0 0 0 0 x x x x x x
0 0 0 0 0 0 0 0 0 x x x x x x
1 0 0 0 0 0 0 0 0 x x x x x x
0 0 0 0 0 0 0 0 0 x x x x x x
1 0 0 0 0 0 0 0 0 x x x x x x
0 0 0 0 0 0 0 0 0 x x x x x x
1 0 0 0 0 0 0 0 0 x x x x x x
0 0 0 0 0 0 0 0 0 x x x x x x
1 0 0 0 0 0 0 0 0 x x x x x x
0 0 0 0 0 0 0 0 0 x x x x x x
1 0 0 0 0 0 0 0 0 x x x x x x
0 0 0 0 0 0 0 0 0 x x x x x x
1 0 0 0 0 0 0 0 0 x x x x x x
0 0 0 0 0 0 0 0 0 x x x x x x
1 0 0 0 0 0 0 0 0 x x x x x x
0 0 0 0 0 0 0 0 0 x x x x x x
1 0 0 0 0 0 0 0 0 x x x x x x
0 0 0 0 0 0 0 0 0 x x x x x x
1 0 0 0 0 0 0 0 0 x x x x x x
0 0 0 0 0 0 0 0 0 x x x x x x
1 0 0 0 0 0 0 0 0 x x x x x x
0 0 0 0 0 0 0 0 0 x x x x x x
1 0 0 0 0 0 0 0 0 x x x x x x
0 0 0 0 0 0 0 0 0 x x x x x x
1 0 0 0 0 0 0 0 0 x x x x x x
0 0 0 0 0 0 0 0 0 x x x x x x
1 0 0 0 0 0 0 0 0 x x x x x x
0 0 0 0 0 0 0 0 0 x x x x x x
1 0 0 0 0 0 0 0 0 x x x x x x
0 0 0 0 0 0 0 0 0 x x x x x x
1 0 0 0 0 0 0 0 0 x x x x x x
0 0 0 0 0 0 0 0 0 x x x x x x
1 0 0 0 0 0 0 0 0 x x x x x x
0 0 0 0 0 0 0 0 0 x x x x x x
1 0 0 0 0 0 0 0 0 x x x x x x
0 0 0 0 0 0 0 0 0 x x x x x x
1 0 0 0 0 0 0 0 0 x x x x x x
0 0 0 0 0 0 0 0 0 x x x x x x
1 0 0 0 0 0 0 0 0 x x x x x x
0 0 0 0 0 0 0 0 0 5 0 0 0 0 0
1 0 0 0 0 0 0 0 0 5 0 0 0 0 0
0 0 0 0 0 0 0 1 0 5 0 0 0 0 0
1 0 0 0 0 0 0 1 0 5 0 0 0 0 0
0 0 0 0 0 0 0 0 0 x x x x x x
1 0 0 0 0 0 0 0 0 x x x x x x
0 0 0 0 0 0 0 0 0 x x x x x x
1 0 0 0 0 0 0 0 0 x x x x x x
0 0 0 0 0 0 0 0 0 x x x x x x
1 0 0 0 0 0 0 0 0 x x x x x x
0 0 0 0 0 0 0 0 0 x x x x x x
1 0 0 0 0 0 0 0 0 x x x x x x
0 0 0 0 0 0 0 0 0 x x x x x x
1 0 0 0 0 0 0 0 0 x x x x x x
0 0 0 0 0 0 0 0 0 x x x x x x
1 0 0 0 0 0 0 0 0 x x x x x x
0 0 0 0 0 0 0 0 0 x x x x x x
1 0 0 0 0 0 0 0 0 x x x x x x
0 0 0 0 0 0 0 0 0 x x x x x x
1 0 0 0 0 0 0 0 0 x x x x x x
0 0 0 0 0 0 0 0 0 x x x x x x
1 0 0 0 0 0 0 0 0 x x x x x x
0 0 0 0 0 0 0 0 0 x x x x x x
1 0 0 0 0 0 0 0 0 x x x x x x
0 0 0 0 0 0 0 0 0 x x x x x x
1 0 0 0 0 0 0 0 0 x x x x x x
0 0 0 0 0 0 0 0 0 x x x x x x
1 0 0 0 0 0 0 0 0 x x x x x x
0 0 0 0 0 0 0 0 0 x x x x x x
1 0 0 0 0 0 0 0 0 x x x x x x
0 0 0 0 0 0 0 0 0 x x x x x x
1 0 0 0 0 0 0 0 0 x x x x x x
0 0 0 0 0 0 0 0 0 x x x x x x
1 0 0 0 0 0 0 0 0 x x x x x x
0 0 0 0 0 0 0 0 0 x x x x x x
1 0 0 0 0 0 0 0 0 x x x x x x
0 0 0 0 0 0 0 0 0 x x x x x x
1 0 0 0 0 0 0 0 0 x x x x x x
0 0 0 0 0 0 0 0 0 x x x x x x
1 0 0 0 0 0 0 0 0 x x x x x x
0 0 0 0 0 0 0 0 0 x x x x x x
1 0 0 0 0 0 0 0 0 x x x x x x
0 0 0 0 0 0 0 0 0 x x x x x x
1 0 0 0 0 0 0 0 0 x x x x x x
0 0 0 0 0 0 0 0 0 0 0 0 1 0 0
1 0 0 0 0 0 0 0 0 0 0 0 1 0 0
0 0 0 1 0 0 0 0 0 0 0 0 1 0 0
1 0 0 1 0 0 0 0 0 0 0 0 1 0 0
0 0 0 0 0 0 0 0 0 x x x x x x
1 0 0 0 0 0 0 0 0 x x x x x x
0 0 0 0 0 0 0 0 0 x x x x x x
1 0 0 0 0 0 0 0 0 x x x x x x
0 0 0 0 0 0 0 0 0 x x x x x x
1 0 0 0 0 0 0 0 0 x x x x x x
0 0 0 0 0 0 0 0 0 x x x x x x
1 0 0 0 0 0 0 0 0 x x x x x x
0 0 0 0 0 0 0 0 0 x x x x x x
1 0 0 0 0 0 0 0 0 x x x x x x
0 0 0 0 0 0 0 0 0 x x x x x x
1 0 0 0 0 0 0 0 0 x x x x x x
0 0 0 0 0 0 0 0 0 x x x x x x
1 0 0 0 0 0 0 0 0 x x x x x x
0 0 0 0 0 0 0 0 0 x x x x x x
1 0 0 0 0 0 0 0 0 x x x x x x
0 0 0 0 0 0 0 0 0 x x x x x x
1 0 0 0 0 0 0 0 0 x x x x x x
0 0 0 0 0 0 0 0 0 x x x x x x
1 0 0 0 0 0 0 0 0 x x x x x x
0 0 0 0 0 0 0 0 0 x x x x x x
1 0 0 0 0 0 0 0 0 x x x x x x
0 0 0 0 0 0 0 0 0 x x x x x x
1 0 0 0 0 0 0 0 0 x x x x x x
0 0 0 0 0 0 0 0 0 x x x x x x
1 0 0 0 0 0 0 0 0 x x x x x x
0 0 0 0 0 0 0 0 0 x x x x x x
1 0 0 0 0 0 0 0 0 x x x x x x
0 0 0 0 0 0 0 0 0 x x x x x x
1 0 0 0 0 0 0 0 0 x x x x x x
0 0 0 0 0 0 0 0 0 x x x x x x
1 0 0 0 0 0 0 0 0 x x x x x x
0 0 0 0 0 0 0 0 0 x x x x x x
1 0 0 0 0 0 0 0 0 x x x x x x
0 0 0 0 0 0 0 0 0 x x x x x x
1 0 0 0 0 0 0 0 0 x x x x x x
0 0 0 0 0 0 0 0 0 x x x x x x
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*/

/* Test case TC4:
clock reset P5 P10 P20 Pcoffee Ptea Pchange Pnext Balance CoffeeOut TeaOut Change5 Change10 Change20
0 1 0 0 0 0 0 0 0 x x x x x x
1 1 0 0 0 0 0 0 0 0 0 0 0 0 0
0 0 0 0 1 0 0 0 0 0 0 0 0 0 0
1 0 0 0 1 0 0 0 0 0 0 0 0 0 0
0 0 0 0 0 0 0 0 0 x x x x x x
1 0 0 0 0 0 0 0 0 x x x x x x
0 0 0 0 0 0 0 0 0 x x x x x x
1 0 0 0 0 0 0 0 0 x x x x x x
0 0 0 0 0 0 0 0 0 x x x x x x
1 0 0 0 0 0 0 0 0 x x x x x x
0 0 0 0 0 0 0 0 0 x x x x x x
1 0 0 0 0 0 0 0 0 x x x x x x
0 0 0 0 0 0 0 0 0 x x x x x x
1 0 0 0 0 0 0 0 0 x x x x x x
0 0 0 0 0 0 0 0 0 x x x x x x
1 0 0 0 0 0 0 0 0 x x x x x x
0 0 0 0 0 0 0 0 0 x x x x x x
1 0 0 0 0 0 0 0 0 x x x x x x
0 0 0 0 0 0 0 0 0 x x x x x x
1 0 0 0 0 0 0 0 0 x x x x x x
0 0 0 0 0 0 0 0 0 x x x x x x
1 0 0 0 0 0 0 0 0 x x x x x x
0 0 0 0 0 0 0 0 0 x x x x x x
1 0 0 0 0 0 0 0 0 x x x x x x
0 0 0 0 0 0 0 0 0 x x x x x x
1 0 0 0 0 0 0 0 0 x x x x x x
0 0 0 0 0 0 0 0 0 x x x x x x
1 0 0 0 0 0 0 0 0 x x x x x x
0 0 0 0 0 0 0 0 0 x x x x x x
1 0 0 0 0 0 0 0 0 x x x x x x
0 0 0 0 0 0 0 0 0 x x x x x x
1 0 0 0 0 0 0 0 0 x x x x x x
0 0 0 0 0 0 0 0 0 x x x x x x
1 0 0 0 0 0 0 0 0 x x x x x x
0 0 0 0 0 0 0 0 0 x x x x x x
1 0 0 0 0 0 0 0 0 x x x x x x
0 0 0 0 0 0 0 0 0 x x x x x x
1 0 0 0 0 0 0 0 0 x x x x x x
0 0 0 0 0 0 0 0 0 x x x x x x
1 0 0 0 0 0 0 0 0 x x x x x x
0 0 0 0 0 0 0 0 0 x x x x x x
1 0 0 0 0 0 0 0 0 x x x x x x
0 0 0 0 0 0 0 0 0 x x x x x x
1 0 0 0 0 0 0 0 0 x x x x x x
0 0 0 0 0 0 0 0 0 20 0 0 0 0 0
1 0 0 0 0 0 0 0 0 20 0 0 0 0 0
0 0 0 0 1 0 0 0 0 20 0 0 0 0 0
1 0 0 0 1 0 0 0 0 20 0 0 0 0 0
0 0 0 0 0 0 0 0 0 x x x x x x
1 0 0 0 0 0 0 0 0 x x x x x x
0 0 0 0 0 0 0 0 0 x x x x x x
1 0 0 0 0 0 0 0 0 x x x x x x
0 0 0 0 0 0 0 0 0 x x x x x x
1 0 0 0 0 0 0 0 0 x x x x x x
0 0 0 0 0 0 0 0 0 x x x x x x
1 0 0 0 0 0 0 0 0 x x x x x x
0 0 0 0 0 0 0 0 0 x x x x x x
1 0 0 0 0 0 0 0 0 x x x x x x
0 0 0 0 0 0 0 0 0 x x x x x x
1 0 0 0 0 0 0 0 0 x x x x x x
0 0 0 0 0 0 0 0 0 x x x x x x
1 0 0 0 0 0 0 0 0 x x x x x x
0 0 0 0 0 0 0 0 0 x x x x x x
1 0 0 0 0 0 0 0 0 x x x x x x
0 0 0 0 0 0 0 0 0 x x x x x x
1 0 0 0 0 0 0 0 0 x x x x x x
0 0 0 0 0 0 0 0 0 x x x x x x
1 0 0 0 0 0 0 0 0 x x x x x x
0 0 0 0 0 0 0 0 0 x x x x x x
1 0 0 0 0 0 0 0 0 x x x x x x
0 0 0 0 0 0 0 0 0 x x x x x x
1 0 0 0 0 0 0 0 0 x x x x x x
0 0 0 0 0 0 0 0 0 x x x x x x
1 0 0 0 0 0 0 0 0 x x x x x x
0 0 0 0 0 0 0 0 0 x x x x x x
1 0 0 0 0 0 0 0 0 x x x x x x
0 0 0 0 0 0 0 0 0 x x x x x x
1 0 0 0 0 0 0 0 0 x x x x x x
0 0 0 0 0 0 0 0 0 x x x x x x
1 0 0 0 0 0 0 0 0 x x x x x x
0 0 0 0 0 0 0 0 0 x x x x x x
1 0 0 0 0 0 0 0 0 x x x x x x
0 0 0 0 0 0 0 0 0 x x x x x x
1 0 0 0 0 0 0 0 0 x x x x x x
0 0 0 0 0 0 0 0 0 x x x x x x
1 0 0 0 0 0 0 0 0 x x x x x x
0 0 0 0 0 0 0 0 0 x x x x x x
1 0 0 0 0 0 0 0 0 x x x x x x
0 0 0 0 0 0 0 0 0 40 0 0 0 0 0
1 0 0 0 0 0 0 0 0 40 0 0 0 0 0
0 0 0 0 0 0 1 0 0 40 0 0 0 0 0
1 0 0 0 0 0 1 0 0 40 0 0 0 0 0
0 0 0 0 0 0 0 0 0 x x x x x x
1 0 0 0 0 0 0 0 0 x x x x x x
0 0 0 0 0 0 0 0 0 x x x x x x
1 0 0 0 0 0 0 0 0 x x x x x x
0 0 0 0 0 0 0 0 0 x x x x x x
1 0 0 0 0 0 0 0 0 x x x x x x
0 0 0 0 0 0 0 0 0 x x x x x x
1 0 0 0 0 0 0 0 0 x x x x x x
0 0 0 0 0 0 0 0 0 x x x x x x
1 0 0 0 0 0 0 0 0 x x x x x x
0 0 0 0 0 0 0 0 0 x x x x x x
1 0 0 0 0 0 0 0 0 x x x x x x
0 0 0 0 0 0 0 0 0 x x x x x x
1 0 0 0 0 0 0 0 0 x x x x x x
0 0 0 0 0 0 0 0 0 x x x x x x
1 0 0 0 0 0 0 0 0 x x x x x x
0 0 0 0 0 0 0 0 0 x x x x x x
1 0 0 0 0 0 0 0 0 x x x x x x
0 0 0 0 0 0 0 0 0 x x x x x x
1 0 0 0 0 0 0 0 0 x x x x x x
0 0 0 0 0 0 0 0 0 x x x x x x
1 0 0 0 0 0 0 0 0 x x x x x x
0 0 0 0 0 0 0 0 0 x x x x x x
1 0 0 0 0 0 0 0 0 x x x x x x
0 0 0 0 0 0 0 0 0 x x x x x x
1 0 0 0 0 0 0 0 0 x x x x x x
0 0 0 0 0 0 0 0 0 x x x x x x
1 0 0 0 0 0 0 0 0 x x x x x x
0 0 0 0 0 0 0 0 0 x x x x x x
1 0 0 0 0 0 0 0 0 x x x x x x
0 0 0 0 0 0 0 0 0 x x x x x x
1 0 0 0 0 0 0 0 0 x x x x x x
0 0 0 0 0 0 0 0 0 x x x x x x
1 0 0 0 0 0 0 0 0 x x x x x x
0 0 0 0 0 0 0 0 0 x x x x x x
1 0 0 0 0 0 0 0 0 x x x x x x
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*/
