// Digital circuit dafuqt3.dig as structural Verilog
module dafuqt3 (
  input  [8:0] N,
  input  reset,
  input  start,
  input  clock,
  output done,
  output [7:0] displayout,
  output [15:0] clockcount,
  output valid
);

  wire and_2_out, and_3_out, and_4_out, and_5_out, CHECKFREQ, comparator_3_eq, DONE_t, LOOPMAP,
       map_value_eq__eq_0, MAPADD, multiplexer_1_out, multiplexer_2_out, multiplexer_5_out,
       multiplexer_6_out, multiplexer_7_out, multiplexer_8_out, N_gt_0, not_1_out, not_2_out, not_3_out,
       not_4_out, not_5_out, not_6_out, NULL, or_1_out, PRESIM, RESET_t, ROM_address_lt_N, SHOWANDPUT, sig,
       sorted_address_lt_N;
  wire [2:0] state;
  wire [7:0] map_address, multiplexer_3_out, multiplexer_4_out, ROM_value, sorted_value;
  wire [8:0] add_1_s, map_value, N_1, ROM_address, sorted_address;
  wire [9:0] lookuptable_1_out;
  wire [9:9] add_1_s_2, sub_1_s;

  Comparator #(.Bits(9)) comparator_1 (.a(ROM_address), .b(N_1), .lt(ROM_address_lt_N));  // open: gt, eq
  Comparator #(.Bits(9)) comparator_2 (.a(N), .b({9{1'b0}}), .gt(N_gt_0));  // open: eq, lt
  Comparator #(.Bits(9)) comparator_3 (.a(map_value), .b({9{1'b0}}), .eq(comparator_3_eq));  // open: gt, lt
  Comparator #(.Bits(9)) comparator_4 (.a(sorted_address), .b(N), .lt(sorted_address_lt_N));  // open: gt, eq
  Sub #(.Bits(10)) sub_1 (.a({1'b0, N}), .b(10'h1), .c_i(1'b0), .s({sub_1_s[9], N_1}));  // open: c_o
  and and_1 (map_value_eq__eq_0, comparator_3_eq, ~MAPADD);  // And
  Multiplexer multiplexer_1 (.sel(RESET_t), .in_0(sig), .in_1(1'b0), .out(multiplexer_1_out));
  Multiplexer multiplexer_2 (.sel(CHECKFREQ), .in_0(multiplexer_1_out), .in_1(1'b1), .out(multiplexer_2_out));
  LookUpTable #(.Bits(10)) lookuptable_1 (.in0(MAPADD), .in1(SHOWANDPUT), .out(lookuptable_1_out));
  D_FF d_ff_1 (.D(multiplexer_2_out), .C(clock), .Q(sig));  // open: nQ
  Add #(.Bits(10)) add_1 (
    .a({1'b0, map_value}), .b(lookuptable_1_out), .c_i(1'b0), .s({add_1_s_2[9], add_1_s}));  // open: c_o
  Multiplexer #(.Bits(8)) multiplexer_3 (.sel(sig), .in_0(ROM_value), .in_1(map_address), .out(multiplexer_3_out));
  or or_1 (or_1_out, MAPADD, SHOWANDPUT);
  ROM #(.AddrBits(9), .isProgramMemory("true"), .Bits(8)) ROMFILE (.A(ROM_address), .sel(1'b1), .D(ROM_value));
  Counter #(.Bits(9)) counter_1 (.en(MAPADD), .C(clock), .clr(RESET_t), .out(ROM_address));  // open: ovf
  RAMDualPort #(.AddrBits(8), .Bits(9)) map (
    .A(multiplexer_3_out), .Din(add_1_s), .str(or_1_out), .C(clock), .ld(1'b1), .D(map_value));
  Counter #(.Bits(8)) counter_2 (.en(LOOPMAP), .C(clock), .clr(RESET_t), .out(map_address));  // open: ovf
  RAMDualPort #(.AddrBits(9), .Bits(8)) RAM (
    .A(sorted_address), .Din(map_address), .str(SHOWANDPUT), .C(clock), .ld(1'b1), .D(sorted_value));
  Counter #(.Bits(9)) counter_3 (.en(SHOWANDPUT), .C(clock), .clr(RESET_t), .out(sorted_address));  // open: ovf
  Seven_Seg_Hex seven_seg_hex_1 (.d(displayout[7:4]), .dp(1'b0));
  Multiplexer #(.Bits(8)) multiplexer_4 (
    .sel(SHOWANDPUT), .in_0({8{1'b0}}), .in_1(map_address), .out(multiplexer_4_out));
  Multiplexer multiplexer_5 (.sel(DONE_t), .in_0(1'b0), .in_1(1'b1), .out(multiplexer_5_out));
  and and_2 (and_2_out, ~DONE_t, ~PRESIM);  // And
  Seven_Seg_Hex seven_seg_hex_2 (.d(displayout[3:0]), .dp(1'b0));
  D_FF #(.Bits(8)) d_ff_2 (.D(multiplexer_4_out), .C(clock), .Q(displayout));  // open: nQ
  D_FF d_ff_3 (.D(SHOWANDPUT), .C(clock), .Q(valid));  // open: nQ
  D_FF d_ff_4 (.D(multiplexer_5_out), .C(clock), .Q(done));  // open: nQ
  Counter #(.Bits(16)) counter_4 (.en(and_2_out), .C(clock), .clr(RESET_t), .out(clockcount));  // open: ovf
  and and_3 (and_3_out, ROM_address_lt_N, N_gt_0);
  and and_4 (and_4_out, ROM_address_lt_N, N_gt_0);
  and and_5 (and_5_out, ROM_address_lt_N, N_gt_0);
  not not_1 (not_1_out, and_3_out);
  not not_2 (not_2_out, reset);
  not not_3 (not_3_out, map_value_eq__eq_0);
  not not_4 (not_4_out, sorted_address_lt_N);
  not not_5 (not_5_out, reset);
  not not_6 (not_6_out, sorted_address_lt_N);
  Multiplexer #(.Selector_Bits(3)) multiplexer_6 (
    .sel(state), .in_0(1'b0), .in_1(1'b0), .in_2(1'b0), .in_3(not_1_out), .in_4(1'b1), .in_5(1'b1),
    .in_6(1'b1), .in_7(not_2_out), .out(multiplexer_6_out));
  D_FF S_2 (.D(multiplexer_6_out), .C(clock), .Q(state[2]));  // open: nQ
  Multiplexer #(.Selector_Bits(3)) multiplexer_7 (
    .sel(state), .in_0(1'b0), .in_1(1'b1), .in_2(1'b1), .in_3(and_4_out), .in_4(not_3_out), .in_5(not_4_out),
    .in_6(1'b0), .in_7(not_5_out), .out(multiplexer_7_out));
  D_FF S_1 (.D(multiplexer_7_out), .C(clock), .Q(state[1]));  // open: nQ
  Multiplexer #(.Selector_Bits(3)) multiplexer_8 (
    .sel(state), .in_0(1'b1), .in_1(1'b0), .in_2(start), .in_3(and_5_out), .in_4(map_value_eq__eq_0),
    .in_5(not_6_out), .in_6(1'b0), .in_7(1'b1), .out(multiplexer_8_out));
  D_FF S_0 (.D(multiplexer_8_out), .C(clock), .Q(state[0]));  // open: nQ
  Demultiplexer #(.Selector_Bits(3)) demultiplexer_1 (
    .sel(state), .in(1'b1), .out_0(NULL), .out_1(RESET_t), .out_2(PRESIM), .out_3(MAPADD), .out_4(CHECKFREQ),
    .out_5(LOOPMAP), .out_6(SHOWANDPUT), .out_7(DONE_t));

  // Other names for the same wires on the sheet: clk = clock

  // Notes on the sheet:
  //   clock: Hz: 100
  //   contents of lookuptable_1 (hex, n*v repeats v):
  //   0,1,ffffffffffffffff
  //   contents of ROMFILE (hex, n*v repeats v):
  //   4,3,1,2,2,2,3,3,4,4,5,5,6,6,7,7,8,8,9,9,10,10,11,11,12,12,13,13
  //   ,14,14,15,15,16,16,17,17,18,18,19,19,20,20,21,21,22,22,23,23,24,24
  //   ,25,25,26,26,27,27,28,28,29,29,30,30,31,31,32,32,33,33,34,34,35,35
  //   ,36,36,37,37,38,38,39,39,40,40,41,41,42,42,43,43,44,44,45,45,46,46
  //   ,47,47,48,48,49,49,50,50,51,51,52,52,53,53,54,54,55,55,56,56,57,57
  //   ,58,58,59,59,60,60,61,61,62,62,63,63,64,64,65,65,66,66,67,67,68,68
  //   ,69,69,70,70,71,71,72,72,73,73,74,74,75,75,76,76,77,77,78,78,79,79
  //   ,80,80,81,81,82,82,83,83,84,84,85,85,86,86,87,87,88,88,89,89,90,90
  //   ,91,91,92,92,93,93,94,94,95,95,96,96,97,97,98,98,99,99,100,100
  //   ,101,101,102,102,103,103,104,104,105,105,106,106,107,107,108,108
  //   ,109,109,110,110,111,111,112,112,113,113,114,114,115,115,116,116
  //   ,117,117,118,118,119,119,120,120,121,121,122,122,123,123,124,124
  //   ,125,125,126,126,127,127,128,128,129,129,130,130,131,131,132,132
  //   ,133,133,134,134,135,135,136,136,137,137,138,138,139,139,140,140
  //   ,141,141,142,142,143,143,144,144,145,145,146,146,147,147,148,148
  //   ,149,149,150,150,151,151,152,152,153,153,154,154,155,155,156,156
  //   ,157,157,158,158,159,159,160,160,161,161,162,162,163,163,164,164
  //   ,165,165,166,166,167,167,168,168,169,169,170,170,171,171,172,172
  //   ,173,173,174,174,175,175,176,176,177,177,178,178,179,179,180,180
  //   ,181,181,182,182,183,183,184,184,185,185,186,186,187,187,188,188
  //   ,189,189,190,190,191,191,192,192,193,193,194,194,195,195,196,196
  //   ,197,197,198,198,199,199,200,200,201,201,202,202,203,203,204,204
  //   ,205,205,206,206,207,207,208,208,209,209,210,210,211,211,212,212
  //   ,213,213,214,214,215,215,216,216,217,217,218,218,219,219,220,220
  //   ,221,221,222,222,223,223,224,224,225,225,226,226,227,227,228,228
  //   ,229,229,230,230,231,231,232,232,233,233,234,234,235,235,236,236
  //   ,237,237,238,238,239,239,240,240,241,241,242,242,243,243,244,244
  //   ,245,245,246,246,247,247,248,248,249,249,250,250,251,251,252,252
  //   ,253,253,254,254,255,f4
endmodule
