// Digital circuit imatmylimit2.dig as structural Verilog
module imatmylimit2 (
  input  [8:0] N,
  input  reset,
  input  start,
  input  clock,
  output done,
  output [7:0] displayout,
  output [15:0] clockcount,
  output valid
);

  wire and_2_out, and_3_out, and_4_out, and_5_out, CHECKFREQ, comparator_3_eq, DONE_t, LOOPMAP,
       map_value_eq__eq_0, MAPADD, multiplexer_3_out, multiplexer_4_out, multiplexer_5_out,
       multiplexer_6_out, N_gt_0, nand_1_out, nand_2_out, not_1_out, not_2_out, not_3_out, not_4_out,
       not_5_out, NULL, or_1_out, PRESIM, RESET_t, ROM_address_lt_N, SHOWANDPUT, sorted_address_lt_N;
  wire [2:0] state;
  wire [7:0] map_address, multiplexer_1_out, multiplexer_2_out, ROM_value, sorted_value;
  wire [8:0] add_1_s, map_value, N_1, ROM_address, sorted_address;
  wire [9:0] lookuptable_1_out;
  wire [9:9] add_1_s_2, sub_1_s;

  Comparator #(.Bits(9)) comparator_1 (.a(ROM_address), .b(N), .lt(ROM_address_lt_N));  // open: gt, eq
  Comparator #(.Bits(9)) comparator_2 (.a(N), .b({9{1'b0}}), .gt(N_gt_0));  // open: eq, lt
  Comparator #(.Bits(9)) comparator_3 (.a(map_value), .b({9{1'b0}}), .eq(comparator_3_eq));  // open: gt, lt
  Comparator #(.Bits(9)) comparator_4 (.a(sorted_address), .b(N), .lt(sorted_address_lt_N));  // open: gt, eq
  Sub #(.Bits(10)) sub_1 (.a({1'b0, N}), .b(10'h1), .c_i(1'b0), .s({sub_1_s[9], N_1}));  // open: c_o
  and and_1 (map_value_eq__eq_0, comparator_3_eq, ~MAPADD);  // And
  LookUpTable #(.Bits(10)) lookuptable_1 (.in0(MAPADD), .in1(SHOWANDPUT), .out(lookuptable_1_out));
  Add #(.Bits(10)) add_1 (
    .a({1'b0, map_value}), .b(lookuptable_1_out), .c_i(1'b0), .s({add_1_s_2[9], add_1_s}));  // open: c_o
  Multiplexer #(.Bits(8)) multiplexer_1 (.sel(MAPADD), .in_0(map_address), .in_1(ROM_value), .out(multiplexer_1_out));
  or or_1 (or_1_out, MAPADD, SHOWANDPUT);
  ROM #(.AddrBits(9), .isProgramMemory("true"), .Bits(8)) ROMFILE (.A(ROM_address), .sel(1'b1), .D(ROM_value));
  Counter #(.Bits(9)) counter_1 (.en(MAPADD), .C(clock), .clr(RESET_t), .out(ROM_address));  // open: ovf
  RAMDualPort #(.AddrBits(8), .Bits(9)) map (
    .A(multiplexer_1_out), .Din(add_1_s), .str(1'b1), .C(clock), .ld(1'b1), .D(map_value));
  Counter #(.Bits(8)) counter_2 (.en(LOOPMAP), .C(clock), .clr(RESET_t), .out(map_address));  // open: ovf
  RAMDualPort #(.AddrBits(9), .Bits(8)) RAM (
    .A(sorted_address), .Din(map_address), .str(1'b1), .C(clock), .ld(1'b1), .D(sorted_value));
  Counter #(.Bits(9)) counter_3 (.en(SHOWANDPUT), .C(clock), .clr(RESET_t), .out(sorted_address));  // open: ovf
  and and_2 (and_2_out, ROM_address_lt_N, N_gt_0);
  and and_3 (and_3_out, ROM_address_lt_N, N_gt_0);
  Seven_Seg_Hex seven_seg_hex_1 (.d(displayout[7:4]), .dp(1'b0));
  Multiplexer #(.Bits(8)) multiplexer_2 (
    .sel(SHOWANDPUT), .in_0({8{1'b0}}), .in_1(map_address), .out(multiplexer_2_out));
  nand nand_1 (nand_1_out, map_value_eq__eq_0, sorted_address_lt_N);
  nand nand_2 (nand_2_out, ~map_value_eq__eq_0, sorted_address_lt_N);  // NAnd
  Multiplexer multiplexer_3 (.sel(DONE_t), .in_0(1'b0), .in_1(1'b1), .out(multiplexer_3_out));
  and and_4 (and_4_out, ~DONE_t, ~PRESIM);  // And
  Seven_Seg_Hex seven_seg_hex_2 (.d(displayout[3:0]), .dp(1'b0));
  D_FF #(.Bits(8)) d_ff_1 (.D(multiplexer_2_out), .C(clock), .Q(displayout));  // open: nQ
  D_FF d_ff_2 (.D(SHOWANDPUT), .C(clock), .Q(valid));  // open: nQ
  D_FF d_ff_3 (.D(multiplexer_3_out), .C(clock), .Q(done));  // open: nQ
  Counter #(.Bits(16)) counter_4 (.en(and_4_out), .C(clock), .clr(RESET_t), .out(clockcount));  // open: ovf
  and and_5 (and_5_out, ROM_address_lt_N, N_gt_0);
  not not_1 (not_1_out, and_5_out);
  not not_2 (not_2_out, reset);
  not not_3 (not_3_out, sorted_address_lt_N);
  not not_4 (not_4_out, reset);
  not not_5 (not_5_out, sorted_address_lt_N);
  Multiplexer #(.Selector_Bits(3)) multiplexer_4 (
    .sel(state), .in_0(1'b0), .in_1(1'b0), .in_2(1'b0), .in_3(not_1_out), .in_4(1'b1), .in_5(1'b1),
    .in_6(1'b1), .in_7(not_2_out), .out(multiplexer_4_out));
  D_FF S_2 (.D(multiplexer_4_out), .C(clock), .Q(state[2]));  // open: nQ
  Multiplexer #(.Selector_Bits(3)) multiplexer_5 (
    .sel(state), .in_0(1'b0), .in_1(1'b1), .in_2(1'b1), .in_3(and_2_out), .in_4(nand_1_out),
    .in_5(not_3_out), .in_6(1'b0), .in_7(not_4_out), .out(multiplexer_5_out));
  D_FF S_1 (.D(multiplexer_5_out), .C(clock), .Q(state[1]));  // open: nQ
  Multiplexer #(.Selector_Bits(3)) multiplexer_6 (
    .sel(state), .in_0(1'b1), .in_1(1'b0), .in_2(start), .in_3(and_3_out), .in_4(nand_2_out),
    .in_5(not_5_out), .in_6(1'b0), .in_7(1'b1), .out(multiplexer_6_out));
  D_FF S_0 (.D(multiplexer_6_out), .C(clock), .Q(state[0]));  // open: nQ
  Demultiplexer #(.Selector_Bits(3)) demultiplexer_1 (
    .sel(state), .in(1'b1), .out_0(NULL), .out_1(RESET_t), .out_2(PRESIM), .out_3(MAPADD), .out_4(CHECKFREQ),
    .out_5(LOOPMAP), .out_6(SHOWANDPUT), .out_7(DONE_t));

  // Other names for the same wires on the sheet: clk = clock

  // Notes on the sheet:
  //   clock: Hz: 100
  //   contents of lookuptable_1 (hex, n*v repeats v):
  //   0,1,ffffffffffffffff
  //   contents of ROMFILE (hex, n*v repeats v):
  //   0,0,1,1,2,2,3,3,4,4,5,5,6,6,7,7,8,8,9,9,a,a,b,b,c,c,d,d,e,e,f,f
  //   ,10,10,11,11,12,12,13,13,14,14,15,15,16,16,17,17,18,18,19,19,1a,1a
  //   ,1b,1b,1c,1c,1d,1d,1e,1e,1f,1f,20,20,21,21,22,22,23,23,24,24,25,25
  //   ,26,26,27,27,28,28,29,29,2a,2a,2b,2b,2c,2c,2d,2d,2e,2e,2f,2f,30,30
  //   ,31,31,32,32,33,33,34,34,35,35,36,36,37,37,38,38,39,39,3a,3a,3b,3b
  //   ,3c,3c,3d,3d,3e,3e,3f,3f,40,40,41,41,42,42,43,43,44,44,45,45,46,46
  //   ,47,47,48,48,49,49,4a,4a,4b,4b,4c,4c,4d,4d,4e,4e,4f,4f,50,50,51,51
  //   ,52,52,53,53,54,54,55,55,56,56,57,57,58,58,59,59,5a,5a,5b,5b,5c,5c
  //   ,5d,5d,5e,5e,5f,5f,60,60,61,61,62,62,63,63,64,64,65,65,66,66,67,67
  //   ,68,68,69,69,6a,6a,6b,6b,6c,6c,6d,6d,6e,6e,6f,6f,70,70,71,71,72,72
  //   ,73,73,74,74,75,75,76,76,77,77,78,78,79,79,7a,7a,7b,7b,7c,7c,7d,7d
  //   ,7e,7e,7f,7f,80,80,81,81,82,82,83,83,84,84,85,85,86,86,87,87,88,88
  //   ,89,89,8a,8a,8b,8b,8c,8c,8d,8d,8e,8e,8f,8f,90,90,91,91,92,92,93,93
  //   ,94,94,95,95,96,96,97,97,98,98,99,99,9a,9a,9b,9b,9c,9c,9d,9d,9e,9e
  //   ,9f,9f,a0,a0,a1,a1,a2,a2,a3,a3,a4,a4,a5,a5,a6,a6,a7,a7,a8,a8,a9,a9
  //   ,aa,aa,ab,ab,ac,ac,ad,ad,ae,ae,af,af,b0,b0,b1,b1,b2,b2,b3,b3,b4,b4
  //   ,b5,b5,b6,b6,b7,b7,b8,b8,b9,b9,ba,ba,bb,bb,bc,bc,bd,bd,be,be,bf,bf
  //   ,c0,c0,c1,c1,c2,c2,c3,c3,c4,c4,c5,c5,c6,c6,c7,c7,c8,c8,c9,c9,ca,ca
  //   ,cb,cb,cc,cc,cd,cd,ce,ce,cf,cf,d0,d0,d1,d1,d2,d2,d3,d3,d4,d4,d5,d5
  //   ,d6,d6,d7,d7,d8,d8,d9,d9,da,da,db,db,dc,dc,dd,dd,de,de,df,df,e0,e0
  //   ,e1,e1,e2,e2,e3,e3,e4,e4,e5,e5,e6,e6,e7,e7,e8,e8,e9,e9,ea,ea,eb,eb
  //   ,ec,ec,ed,ed,ee,ee,ef,ef,f0,f0,f1,f1,f2,f2,f3,f3,f4,f4,f5,f5,f6,f6
  //   ,f7,f7,f8,f8,f9,f9,fa,fa,fb,fb,fc,fc,fd,fd,fe,fe,ff,a
endmodule
