// Digital circuit orgasmfix0.dig as structural Verilog
module orgasmfix0 (
  input  [8:0] N,
  input  reset,
  input  start,
  input  clock,
  output done,
  output [7:0] displayout,
  output [15:0] clockcount,
  output valid
);

  wire and_2_out, and_3_out, and_4_out, and_5_out, CHECKFREQ, comparator_3_eq, DONE_t, LOOPMAP,
       map_value_eq__eq_0, MAPADD, multiplexer_3_out, multiplexer_4_out, multiplexer_5_out,
       multiplexer_6_out, N_gt_0, not_1_out, not_2_out, not_3_out, not_4_out, not_5_out, not_6_out, NULL,
       or_1_out, PRESIM, RESET_t, ROM_address_lt_N_1, SHOWANDPUT, sorted_address_lt_N;
  wire [2:0] state;
  wire [7:0] map_address, multiplexer_1_out, multiplexer_2_out, ROM_value, sorted_value;
  wire [8:0] add_1_s, map_value, N_1, ROM_address, sorted_address;
  wire [9:0] lookuptable_1_out;
  wire [9:9] add_1_s_2, sub_1_s;

  Comparator #(.Bits(9)) comparator_1 (.a(ROM_address), .b(N_1), .lt(ROM_address_lt_N_1));  // open: gt, eq
  Comparator #(.Bits(9)) comparator_2 (.a(N), .b({9{1'b0}}), .gt(N_gt_0));  // open: eq, lt
  Comparator #(.Bits(9)) comparator_3 (.a(map_value), .b({9{1'b0}}), .eq(comparator_3_eq));  // open: gt, lt
  Comparator #(.Bits(9)) comparator_4 (.a(sorted_address), .b(N), .lt(sorted_address_lt_N));  // open: gt, eq
  Sub #(.Bits(10)) sub_1 (.a({1'b0, N}), .b(10'h1), .c_i(1'b0), .s({sub_1_s[9], N_1}));  // open: c_o
  and and_1 (map_value_eq__eq_0, comparator_3_eq, ~MAPADD);  // And
  LookUpTable #(.Bits(10)) lookuptable_1 (.in0(MAPADD), .in1(SHOWANDPUT), .out(lookuptable_1_out));
  Add #(.Bits(10)) add_1 (
    .a({1'b0, map_value}), .b(lookuptable_1_out), .c_i(1'b0), .s({add_1_s_2[9], add_1_s}));  // open: c_o
  Multiplexer #(.Bits(8)) multiplexer_1 (.sel(MAPADD), .in_0(map_address), .in_1(ROM_value), .out(multiplexer_1_out));
  or or_1 (or_1_out, MAPADD, SHOWANDPUT);
  ROM #(.AddrBits(9), .isProgramMemory("true"), .Bits(8)) ROMFILE (.A(ROM_address), .sel(1'b1), .D(ROM_value));
  Counter #(.Bits(9)) counter_1 (.en(MAPADD), .C(clock), .clr(RESET_t), .out(ROM_address));  // open: ovf
  RAMDualPort #(.AddrBits(8), .Bits(9)) map (
    .A(multiplexer_1_out), .Din(add_1_s), .str(or_1_out), .C(clock), .ld(1'b1), .D(map_value));
  Counter #(.Bits(8)) counter_2 (.en(LOOPMAP), .C(clock), .clr(RESET_t), .out(map_address));  // open: ovf
  RAMDualPort #(.AddrBits(9), .Bits(8)) RAM (
    .A(sorted_address), .Din(map_address), .str(SHOWANDPUT), .C(clock), .ld(1'b1), .D(sorted_value));
  Counter #(.Bits(9)) counter_3 (.en(SHOWANDPUT), .C(clock), .clr(RESET_t), .out(sorted_address));  // open: ovf
  Seven_Seg_Hex seven_seg_hex_1 (.d(displayout[7:4]), .dp(1'b0));
  Multiplexer #(.Bits(8)) multiplexer_2 (
    .sel(SHOWANDPUT), .in_0({8{1'b0}}), .in_1(map_address), .out(multiplexer_2_out));
  Multiplexer multiplexer_3 (.sel(DONE_t), .in_0(1'b0), .in_1(1'b1), .out(multiplexer_3_out));
  and and_2 (and_2_out, ~DONE_t, ~PRESIM);  // And
  Seven_Seg_Hex seven_seg_hex_2 (.d(displayout[3:0]), .dp(1'b0));
  D_FF #(.Bits(8)) d_ff_1 (.D(multiplexer_2_out), .C(clock), .Q(displayout));  // open: nQ
  D_FF d_ff_2 (.D(SHOWANDPUT), .C(clock), .Q(valid));  // open: nQ
  D_FF d_ff_3 (.D(multiplexer_3_out), .C(clock), .Q(done));  // open: nQ
  Counter #(.Bits(16)) counter_4 (.en(and_2_out), .C(clock), .clr(RESET_t), .out(clockcount));  // open: ovf
  and and_3 (and_3_out, ROM_address_lt_N_1, N_gt_0);
  and and_4 (and_4_out, ROM_address_lt_N_1, N_gt_0);
  and and_5 (and_5_out, ROM_address_lt_N_1, N_gt_0);
  not not_1 (not_1_out, and_3_out);
  not not_2 (not_2_out, reset);
  not not_3 (not_3_out, map_value_eq__eq_0);
  not not_4 (not_4_out, sorted_address_lt_N);
  not not_5 (not_5_out, reset);
  not not_6 (not_6_out, sorted_address_lt_N);
  Multiplexer #(.Selector_Bits(3)) multiplexer_4 (
    .sel(state), .in_0(1'b0), .in_1(1'b0), .in_2(1'b0), .in_3(not_1_out), .in_4(1'b1), .in_5(1'b1),
    .in_6(1'b1), .in_7(not_2_out), .out(multiplexer_4_out));
  D_FF S_2 (.D(multiplexer_4_out), .C(clock), .Q(state[2]));  // open: nQ
  Multiplexer #(.Selector_Bits(3)) multiplexer_5 (
    .sel(state), .in_0(1'b0), .in_1(1'b1), .in_2(1'b1), .in_3(and_4_out), .in_4(not_3_out), .in_5(not_4_out),
    .in_6(1'b0), .in_7(not_5_out), .out(multiplexer_5_out));
  D_FF S_1 (.D(multiplexer_5_out), .C(clock), .Q(state[1]));  // open: nQ
  Multiplexer #(.Selector_Bits(3)) multiplexer_6 (
    .sel(state), .in_0(1'b1), .in_1(1'b0), .in_2(start), .in_3(and_5_out), .in_4(map_value_eq__eq_0),
    .in_5(not_6_out), .in_6(1'b0), .in_7(1'b1), .out(multiplexer_6_out));
  D_FF S_0 (.D(multiplexer_6_out), .C(clock), .Q(state[0]));  // open: nQ
  Demultiplexer #(.Selector_Bits(3)) demultiplexer_1 (
    .sel(state), .in(1'b1), .out_0(NULL), .out_1(RESET_t), .out_2(PRESIM), .out_3(MAPADD), .out_4(CHECKFREQ),
    .out_5(LOOPMAP), .out_6(SHOWANDPUT), .out_7(DONE_t));

  // Other names for the same wires on the sheet: clk = clock

  // Notes on the sheet:
  //   clock: Hz: 100
  //   contents of lookuptable_1 (hex, n*v repeats v):
  //   0,1,ffffffffffffffff
  //   contents of ROMFILE (hex, n*v repeats v):
  //   512*1
endmodule
