// Digital circuit Template.dig as structural Verilog
module Template (
  input  P,
  input  T,
  input  D,
  input  C,
  input  B,
  input  A,
  input  Clr,
  input  Load,
  input  Clock,
  output QD,
  output QC,
  output QB,
  output QA,
  output RCO
);

  wire and_2_out, and_3_out, and_4_out, and_5_out, and_6_out, and_7_out, and_8_out, and_9_out, and_10_out,
       clrWithCon, driver_1_out, driver_2_out, driver_3_out, driver_4_out, driver_5_out, driver_6_out,
       driver_7_out, driver_8_out, driver_9_out, driver_10_out, driver_11_out, driver_12_out, En, not_1_out,
       not_2_out, not_3_out, not_4_out, not_5_out, or_1_out, or_2_out, or_3_out;

  and and_1 (En, P, T, Load);
  not not_1 (not_1_out, Clr);
  nand nand_1 (clrWithCon, not_1_out, Load);
  not not_2 (not_2_out, QD);
  not not_3 (not_3_out, QC);
  not not_4 (not_4_out, QB);
  not not_5 (not_5_out, QA);
  and and_2 (and_2_out, QA, QB, QC, not_2_out);
  and and_3 (and_3_out, not_5_out, QD);
  and and_4 (and_4_out, not_4_out, QD);
  and and_5 (and_5_out, not_3_out, QD);
  and and_6 (and_6_out, QA, QB, not_3_out);
  and and_7 (and_7_out, not_5_out, QC);
  and and_8 (and_8_out, not_4_out, QC);
  and and_9 (and_9_out, QA, not_4_out);
  and and_10 (and_10_out, not_5_out, QB);
  or or_1 (or_1_out, and_2_out, and_3_out, and_4_out, and_5_out);
  or or_2 (or_2_out, and_6_out, and_7_out, and_8_out);
  or or_3 (or_3_out, and_9_out, and_10_out);
  assign driver_1_out = Load ? QD : 1'bz;  // Driver driver_1
  assign driver_1_out = ~Load ? D : 1'bz;  // DriverInvSel driverinvsel_1
  assign driver_2_out = Load ? QC : 1'bz;  // Driver driver_2
  assign driver_2_out = ~Load ? C : 1'bz;  // DriverInvSel driverinvsel_2
  assign driver_3_out = Load ? QB : 1'bz;  // Driver driver_3
  assign driver_3_out = ~Load ? B : 1'bz;  // DriverInvSel driverinvsel_3
  assign driver_4_out = Load ? QA : 1'bz;  // Driver driver_4
  assign driver_4_out = ~Load ? A : 1'bz;  // DriverInvSel driverinvsel_4
  assign driver_5_out = En ? or_1_out : 1'bz;  // Driver driver_5
  assign driver_5_out = ~En ? driver_1_out : 1'bz;  // DriverInvSel driverinvsel_5
  assign driver_6_out = En ? or_2_out : 1'bz;  // Driver driver_6
  assign driver_6_out = ~En ? driver_2_out : 1'bz;  // DriverInvSel driverinvsel_6
  assign driver_7_out = En ? or_3_out : 1'bz;  // Driver driver_7
  assign driver_7_out = ~En ? driver_3_out : 1'bz;  // DriverInvSel driverinvsel_7
  assign driver_8_out = En ? not_5_out : 1'bz;  // Driver driver_8
  assign driver_8_out = ~En ? driver_4_out : 1'bz;  // DriverInvSel driverinvsel_8
  assign driver_9_out = clrWithCon ? driver_5_out : 1'bz;  // Driver driver_9
  assign driver_9_out = ~clrWithCon ? 1'b0 : 1'bz;  // DriverInvSel driverinvsel_9
  assign driver_10_out = clrWithCon ? driver_6_out : 1'bz;  // Driver driver_10
  assign driver_10_out = ~clrWithCon ? 1'b0 : 1'bz;  // DriverInvSel driverinvsel_10
  assign driver_11_out = clrWithCon ? driver_7_out : 1'bz;  // Driver driver_11
  assign driver_11_out = ~clrWithCon ? 1'b0 : 1'bz;  // DriverInvSel driverinvsel_11
  assign driver_12_out = clrWithCon ? driver_8_out : 1'bz;  // Driver driver_12
  assign driver_12_out = ~clrWithCon ? 1'b0 : 1'bz;  // DriverInvSel driverinvsel_12
  D_FF d_ff_1 (.D(driver_9_out), .C(Clock), .Q(QD));  // open: nQ
  D_FF d_ff_2 (.D(driver_10_out), .C(Clock), .Q(QC));  // open: nQ
  D_FF d_ff_3 (.D(driver_11_out), .C(Clock), .Q(QB));  // open: nQ
  D_FF d_ff_4 (.D(driver_12_out), .C(Clock), .Q(QA));  // open: nQ
  and and_11 (RCO, QD, QC, QB, QA);

  // Other names for the same wires on the sheet: QA_n = QA; QB_n = QB; QC_n = QC; QD_n = QD
endmodule
