// Digital circuit Tem.dig as structural Verilog
module Tem (
  input  P,
  input  Clr,
  input  clock,
  output Z
);

  wire and_1_out, and_2_out, not_1_out, Z_0_n;

  and and_1 (and_1_out, P, ~Clr);  // And
  not not_1 (not_1_out, Z_0_n);
  and and_2 (and_2_out, and_1_out, not_1_out);
  D_FF u_Z_0_n (.D(and_1_out), .C(clock), .Q(Z_0_n));  // open: nQ
  D_FF Z_0_n_2 (.D(and_2_out), .C(clock), .Q(Z));  // open: nQ
endmodule
