// Digital circuit template.dig as structural Verilog
module template (
  input  P,
  input  Clr,
  input  clock,
  output Z
);

  wire and_1_out, and_2_out, and_3_out, not_1_out, not_2_out, not_4_out, or_1_out, STATE0_n, STATE1_n;

  not not_1 (not_1_out, Clr);
  not not_2 (not_2_out, STATE1_n);
  not not_3 (not_2_out, STATE1_n);
  not not_4 (not_4_out, STATE0_n);
  not not_5 (not_4_out, STATE0_n);
  and and_1 (and_1_out, P, STATE1_n, not_1_out);
  and and_2 (and_2_out, STATE0_n, not_1_out);
  and and_3 (and_3_out, P, not_4_out, not_2_out, not_1_out);
  and and_4 (Z, STATE0_n, not_1_out);
  or or_1 (or_1_out, and_1_out, and_2_out);
  D_FF u_STATE1_n (.D(or_1_out), .C(clock), .Q(STATE1_n));  // open: nQ
  D_FF u_STATE0_n (.D(and_3_out), .C(clock), .Q(STATE0_n));  // open: nQ

  // Other names for the same wires on the sheet: clk = clock
endmodule
