// Digital circuit 2557.dig as structural Verilog
module _2557 (
  input  [3:0] V,
  input  [3:0] D,
  input  start,
  input  clk,
  input  reset,
  input  in,
  input  C,
  output Z,
  output busy
);

  wire and_1_out, and_2_out, and_3_out, and_4_out, and_5_out, DIVIDE, IDLE, multiplexer_3_out,
       multiplexer_4_out, not_1_out, not_2_out, not_3_out, NULL, or_1_out, or_2_out, RESET_t, s0, s1, Z_1_n;
  wire [3:0] multiplexer_1_out, multiplexer_2_out, q_q, r_q;

  not not_1 (not_1_out, Z_1_n);
  not not_2 (not_2_out, Z);
  and and_1 (and_1_out, Z, in);
  and and_2 (and_2_out, Z_1_n, in);
  and and_3 (and_3_out, not_2_out, not_1_out, in);
  or or_1 (or_1_out, and_1_out, and_2_out);
  D_FF u_Z_1_n (.D(or_1_out), .C(C), .Q(Z_1_n));  // open: nQ
  D_FF Z_0_n (.D(and_3_out), .C(C), .Q(Z));  // open: nQ
  // Probe state on {Z_1_n, Z}
  and and_4 (and_4_out, IDLE, start);
  or or_2 (or_2_out, and_4_out, DIVIDE);
  D_FF d_ff_1 (.D(or_2_out), .Q(busy));  // open: C, nQ
  and and_5 (and_5_out, ~reset, start);  // And
  not not_3 (not_3_out, reset);
  Div div_1 ();  // open: a, b, q, r
  Multiplexer #(.Bits(4)) multiplexer_1 (.sel(RESET_t), .in_1(4'b0000), .out(multiplexer_1_out));  // open: in_0
  Multiplexer #(.Bits(4)) multiplexer_2 (.sel(RESET_t), .in_1(4'b0000), .out(multiplexer_2_out));  // open: in_0
  Multiplexer #(.Selector_Bits(2)) multiplexer_3 (
    .sel({s1, s0}), .in_0(1'b0), .in_1(and_5_out), .in_2(1'b0), .in_3(1'b0), .out(multiplexer_3_out));
  Multiplexer #(.Selector_Bits(2)) multiplexer_4 (
    .sel({s1, s0}), .in_0(1'b1), .in_1(not_3_out), .in_2(1'b0), .in_3(1'b1), .out(multiplexer_4_out));
  D_FF #(.Bits(4)) r (.D(multiplexer_1_out), .Q(r_q));  // open: C, nQ
  D_FF #(.Bits(4)) q (.D(multiplexer_2_out), .Q(q_q));  // open: C, nQ
  D_FF d_ff_2 (.D(multiplexer_3_out), .C(clk), .Q(s1));  // open: nQ
  D_FF d_ff_3 (.D(multiplexer_4_out), .C(clk), .Q(s0));  // open: nQ
  Demultiplexer #(.Selector_Bits(2)) demultiplexer_1 (
    .sel({s1, s0}), .in(1'b1), .out_0(RESET_t), .out_1(IDLE), .out_2(NULL), .out_3(DIVIDE));

  // Other names for the same wires on the sheet: state[1:0] = {s1, s0}; Z_0_n = Z

  // Notes on the sheet:
  //   C: Hz: 2
endmodule
