// Digital circuit smokeOnTheWater2.dig as structural Verilog
module smokeOnTheWater2 (
  input  [15:0] A,
  input  \input ,
  input  clk,
  output [7:0] sqrt,
  output busy,
  output [7:0] out_6
);

  wire A_gt__eq_C_C, and_1_out, and_2_out, and_3_out, comparator_1_gt, COUNT, IDLE, multiplexer_4_out,
       multiplexer_5_out, not_1_out, not_2_out, not_4_out, or_1_out, RESET, s0, s1, SHOW, start, Z_1_n;
  wire [7:0] multiplexer_1_out, multiplexer_2_out, multiplexer_3_out, multiplexer_6_out, plus_1_s;
  wire [8:0] sub_1_s;
  wire [15:0] C_C;

  not not_1 (not_1_out, Z_1_n);
  not not_2 (not_2_out, start);
  and and_1 (and_1_out, start, \input );
  and and_2 (and_2_out, Z_1_n, \input );
  and and_3 (and_3_out, not_2_out, not_1_out, \input );
  or or_1 (or_1_out, and_1_out, and_2_out);
  D_FF u_Z_1_n (.D(or_1_out), .C(clk), .Q(Z_1_n));  // open: nQ
  D_FF Z_0_n (.D(and_3_out), .C(clk), .Q(start));  // open: nQ
  Add #(.Bits(8)) plus_1 (.a(out_6), .b(8'h1), .c_i(1'b0), .s(plus_1_s));  // open: c_o
  Multiplexer #(.Bits(8)) multiplexer_1 (.sel(COUNT), .in_0(out_6), .in_1(plus_1_s), .out(multiplexer_1_out));
  Multiplexer #(.Bits(8)) multiplexer_2 (.sel(RESET), .in_0(multiplexer_1_out), .in_1(8'h1), .out(multiplexer_2_out));
  D_FF #(.Bits(8)) C (.D(multiplexer_2_out), .C(clk), .Q(out_6));  // open: nQ
  Comparator #(.Bits(16)) comparator_1 (.a(C_C), .b(A), .gt(comparator_1_gt));  // open: eq, lt
  not not_3 (A_gt__eq_C_C, comparator_1_gt);
  Mul #(.Bits(8)) mul_1 (.a(out_6), .b(out_6), .mul(C_C));
  Sub #(.Bits(9)) sub_1 (.a({1'b0, out_6}), .b(9'h1), .c_i(1'b0), .s(sub_1_s));  // open: c_o
  Multiplexer #(.Bits(8)) multiplexer_3 (.sel(SHOW), .in_0(sqrt), .in_1(sub_1_s[7:0]), .out(multiplexer_3_out));
  not not_4 (not_4_out, IDLE);
  Multiplexer #(.Selector_Bits(2)) multiplexer_4 (
    .sel({s1, s0}), .in_0(1'b0), .in_1(1'b1), .in_2(A_gt__eq_C_C), .in_3(1'b1), .out(multiplexer_4_out));
  Multiplexer #(.Selector_Bits(2)) multiplexer_5 (
    .sel({s1, s0}), .in_0(start), .in_1(1'b0), .in_2(A_gt__eq_C_C), .in_3(1'b0), .out(multiplexer_5_out));
  Multiplexer #(.Bits(8)) multiplexer_6 (
    .sel(RESET), .in_0(multiplexer_3_out), .in_1({8{1'b0}}), .out(multiplexer_6_out));
  D_FF d_ff_1 (.D(multiplexer_4_out), .C(clk), .Q(s1));  // open: nQ
  D_FF d_ff_2 (.D(multiplexer_5_out), .C(clk), .Q(s0));  // open: nQ
  D_FF d_ff_3 (.D(not_4_out), .C(clk), .Q(busy));  // open: nQ
  D_FF #(.Bits(8)) d_ff_4 (.D(multiplexer_6_out), .C(clk), .Q(sqrt));  // open: nQ
  Demultiplexer #(.Selector_Bits(2)) demultiplexer_1 (
    .sel({s1, s0}), .in(1'b1), .out_0(IDLE), .out_1(RESET), .out_2(SHOW), .out_3(COUNT));

  // Other names for the same wires on the sheet: C[7:0] = out_6; state[1:0] = {s1, s0}; Z_0_n = start

  // Notes on the sheet:
  //   clk: Hz: 5
endmodule

/* Test case TestCase1:
clk A input sqrt busy
0 0 0 0 0
1 0 0 0 0
0 0 0 0 0
1 0 0 0 0
0 0 1 X X
1 0 1 X X
loop(x,1000)
0 0 0 X X
1 0 0 X X
end loop
0 0 0 0 0
1 0 0 0 0
*/

/* Test case TestCase2:
clk A input sqrt busy
0 0 0 0 0
1 0 0 0 0
0 0 0 0 0
1 0 0 0 0
0 1 1 X X
1 1 1 X X
loop(x,1000)
0 1 0 X X
1 1 0 X X
end loop
0 0 0 1 0
1 0 0 1 0
*/

/* Test case TestCase3:
clk A input sqrt busy
0 0 0 0 0
1 0 0 0 0
0 0 0 0 0
1 0 0 0 0
0 4 1 X X
1 4 1 X X
loop(x,1000)
0 4 0 X X
1 4 0 X X
end loop
0 0 0 2 0
1 0 0 2 0
*/

/* Test case TestCase4:
clk A input sqrt busy
0 0 0 0 0
1 0 0 0 0
0 0 0 0 0
1 0 0 0 0
0 9 1 X X
1 9 1 X X
loop(x,1000)
0 9 0 X X
1 9 0 X X
end loop
0 0 0 3 0
1 0 0 3 0
*/

/* Test case TestCase5:
clk A input sqrt busy
0 0 0 0 0
1 0 0 0 0
0 0 0 0 0
1 0 0 0 0
0 8 1 X X
1 8 1 X X
loop(x,1000)
0 8 0 X X
1 8 0 X X
end loop
0 0 0 2 0
1 0 0 2 0
*/
