// Digital circuit template_01.dig as structural Verilog
module template_01 (
  input  reset,
  input  clk,
  output A,
  output B,
  output C
);

  wire and_1_out, and_2_out, and_3_out, and_4_out, and_5_out, and_6_out, and_7_out, and_8_out, and_9_out,
       not_1_out, not_2_out, not_3_out, or_1_out, or_2_out, or_3_out;

  not not_1 (not_1_out, C);
  not not_2 (not_2_out, B);
  not not_3 (not_3_out, A);
  and and_1 (and_1_out, not_3_out, B);
  and and_2 (and_2_out, A, C);
  and and_3 (and_3_out, A, not_1_out);
  and and_4 (and_4_out, not_3_out, B);
  and and_5 (and_5_out, not_2_out, not_1_out);
  and and_6 (and_6_out, B, C);
  or or_1 (or_1_out, and_1_out, and_2_out);
  or or_2 (or_2_out, and_3_out, and_4_out);
  or or_3 (or_3_out, and_5_out, and_6_out);
  and and_7 (and_7_out, or_1_out, ~reset);  // And
  and and_8 (and_8_out, or_2_out, ~reset);  // And
  and and_9 (and_9_out, or_3_out, ~reset);  // And
  D_FF Q_2_n (.D(and_7_out), .C(clk), .Q(C));  // open: nQ
  D_FF Q_1_n (.D(and_8_out), .C(clk), .Q(B));  // open: nQ
  D_FF Q_0_n (.D(and_9_out), .C(clk), .Q(A));  // open: nQ

  // Other names for the same wires on the sheet: Q_0_n = A; Q_1_n = B; Q_2_n = C
endmodule

/* Test case TestCase:
clk reset C B A
0 0 0 0 0 
0 1 0 0 0
1 1 0 0 0
0 0 0 0 0
1 0 0 0 1
0 0 0 0 1
1 0 0 1 1
0 0 0 1 1
1 0 0 1 0
0 0 0 1 0
1 0 1 1 0
0 0 1 1 0
1 0 1 1 1
0 0 1 1 1
1 0 1 0 1
0 0 1 0 1
1 0 1 0 0
0 0 1 0 0
1 0 0 0 0
0 0 0 0 0
1 0 0 0 1
0 0 0 0 1
1 0 0 1 1
0 0 0 1 1
1 0 0 1 0
0 0 0 1 0
1 0 1 1 0
0 0 1 1 0
1 0 1 1 1
0 0 1 1 1
1 0 1 0 1
0 0 1 0 1
1 0 1 0 0
0 0 1 0 0
*/
