// Digital circuit template_03.dig as structural Verilog
module template_03 (
  input  [15:0] A,
  input  \input ,
  input  clk,
  input  reset,
  output [15:0] mean,
  output [31:0] out_6,
  output busy
);

  wire ADD, add_t, and_1_out, and_2_out, and_3_out, and_4_out, and_5_out, IDLE, multiplexer_1_out,
       multiplexer_2_out, not_1_out, not_2_out, not_3_out, NULL, or_1_out, RESET_t, s0, s1, Z_1_n;
  wire [31:0] add_1_s, add_2_s, add_3_s, div_1_q, multiplexer_3_out, multiplexer_4_out, multiplexer_5_out,
       multiplexer_6_out, N;
  wire [31:16] M;

  not not_1 (not_1_out, Z_1_n);
  not not_2 (not_2_out, add_t);
  and and_1 (and_1_out, add_t, \input );
  and and_2 (and_2_out, Z_1_n, \input );
  and and_3 (and_3_out, not_2_out, not_1_out, \input );
  or or_1 (or_1_out, and_1_out, and_2_out);
  D_FF u_Z_1_n (.D(or_1_out), .C(clk), .Q(Z_1_n));  // open: nQ
  D_FF Z_0_n (.D(and_3_out), .C(clk), .Q(add_t));  // open: nQ
  and and_4 (and_4_out, ~reset, \input );  // And
  not not_3 (not_3_out, reset);
  and and_5 (and_5_out, IDLE, \input );
  Multiplexer #(.Selector_Bits(2)) multiplexer_1 (
    .sel({s1, s0}), .in_0(1'b0), .in_1(and_4_out), .in_2(1'b0), .in_3(1'b0), .out(multiplexer_1_out));
  Multiplexer #(.Selector_Bits(2)) multiplexer_2 (
    .sel({s1, s0}), .in_0(1'b1), .in_1(not_3_out), .in_2(1'b0), .in_3(1'b1), .out(multiplexer_2_out));
  D_FF d_ff_1 (.D(multiplexer_1_out), .C(clk), .Q(s1));  // open: nQ
  D_FF d_ff_2 (.D(multiplexer_2_out), .C(clk), .Q(s0));  // open: nQ
  D_FF d_ff_3 (.D(and_5_out), .C(clk), .Q(busy));  // open: nQ
  Demultiplexer #(.Selector_Bits(2)) demultiplexer_1 (
    .sel({s1, s0}), .in(1'b1), .out_0(RESET_t), .out_1(IDLE), .out_2(NULL), .out_3(ADD));
  Add #(.Bits(32)) add_1 (.a(out_6), .b({{16{1'b0}}, A}), .c_i(1'b0), .s(add_1_s));  // open: c_o
  Add #(.Bits(32)) add_2 (.a(32'h1), .b(N), .c_i(1'b0), .s(add_2_s));  // open: c_o
  Add #(.Bits(32)) add_3 (.a(out_6), .b({{16{1'b0}}, A}), .c_i(1'b0), .s(add_3_s));  // open: c_o
  Div #(.Bits(32)) div_1 (.a(add_1_s), .b(add_2_s), .q(div_1_q));  // open: r
  CounterPreset #(.Bits(32)) counterpreset_1 (
    .en(ADD), .C(clk), .dir(1'b0), .in({32{1'b0}}), .ld(1'b0), .clr(RESET_t), .out(N));  // open: ovf
  Multiplexer #(.Bits(32)) multiplexer_3 (.sel(ADD), .in_0(out_6), .in_1(add_3_s), .out(multiplexer_3_out));
  Multiplexer #(.Bits(32)) multiplexer_4 (.sel(ADD), .in_0({M, mean}), .in_1(div_1_q), .out(multiplexer_4_out));
  Multiplexer #(.Bits(32)) multiplexer_5 (
    .sel(RESET_t), .in_0(multiplexer_3_out), .in_1({32{1'b0}}), .out(multiplexer_5_out));
  Multiplexer #(.Bits(32)) multiplexer_6 (
    .sel(RESET_t), .in_0(multiplexer_4_out), .in_1({32{1'b0}}), .out(multiplexer_6_out));
  D_FF #(.Bits(32)) d_ff_4 (.D(multiplexer_5_out), .C(clk), .Q(out_6));  // open: nQ
  D_FF #(.Bits(32)) d_ff_5 (.D(multiplexer_6_out), .C(clk), .Q({M, mean}));  // open: nQ

  // Other names for the same wires on the sheet: A_t[15:0] = A; Z_0_n = add_t; M[15:0] = mean; state[1:0] = {s1, s0};
  //   T[31:0] = out_6
endmodule

/* Test case Case1:
clk A input reset mean busy
0 0 0 0 0 0
1 0 0 0 0 0
0 0 0 1 0 0
1 0 0 1 0 0
0 0 0 0 0 0
1 0 0 0 0 0
0 5 1 0 X X
1 5 1 0 X X
0 5 0 0 X X
1 5 0 0 X X
loop(x,500)
end loop
0 0 0 0 5 0
1 0 0 0 5 0
*/

/* Test case Case2:
clk A input reset mean busy
0 0 0 0 0 0
1 0 0 0 0 0
0 0 0 1 0 0
1 0 0 1 0 0
0 0 0 0 0 0
1 0 0 0 0 0
0 5 1 0 X X
1 5 1 0 X X
0 5 0 0 X X
1 5 0 0 X X
loop(x,500)
end loop
0 0 0 0 5 0
1 0 0 0 5 0
0 15 1 0 X X
1 15 1 0 X X
0 15 0 0 X X
1 15 0 0 X X
loop(x,500)
end loop
0 0 0 0 10 0
1 0 0 0 10 0
*/

/* Test case Case3:
clk A input reset mean busy
0 0 0 0 0 0
1 0 0 0 0 0
0 0 0 1 0 0
1 0 0 1 0 0
0 0 0 0 0 0
1 0 0 0 0 0
0 65535 1 0 X X
1 65535 1 0 X X
0 65535 0 0 X X
1 65535 0 0 X X
loop(x,500)
end loop
0 0 0 0 65535 0
1 0 0 0 65535 0
0 65535 1 0 X X
1 65535 1 0 X X
0 65535 0 0 X X
1 65535 0 0 X X
loop(x,500)
end loop
0 0 0 0 65535 0
1 0 0 0 65535 0
*/

/* Test case Case4:
clk A input reset mean busy
0 0 0 0 0 0
1 0 0 0 0 0
0 0 0 1 0 0
1 0 0 1 0 0
0 0 0 0 0 0
1 0 0 0 0 0
0 1 1 0 X X
1 1 1 0 X X
0 1 0 0 X X
1 1 0 0 X X
loop(x,500)
end loop
0 0 0 0 1 0
1 0 0 0 1 0
0 2 1 0 X X
1 2 1 0 X X
0 2 0 0 X X
1 2 0 0 X X
loop(x,500)
end loop
0 0 0 0 1 0
1 0 0 0 1 0
0 3 1 0 X X
1 3 1 0 X X
0 3 0 0 X X
1 3 0 0 X X
loop(x,500)
end loop
0 0 0 0 2 0
1 0 0 0 2 0
0 4 1 0 X X
1 4 1 0 X X
0 4 0 0 X X
1 4 0 0 X X
loop(x,500)
end loop
0 0 0 0 2 0
1 0 0 0 2 0
0 5 1 0 X X
1 5 1 0 X X
0 5 0 0 X X
1 5 0 0 X X
loop(x,500)
end loop
0 0 0 0 3 0
1 0 0 0 3 0
0 6 1 0 X X
1 6 1 0 X X
0 6 0 0 X X
1 6 0 0 X X
loop(x,500)
end loop
0 0 0 0 3 0
1 0 0 0 3 0
0 7 1 0 X X
1 7 1 0 X X
0 7 0 0 X X
1 7 0 0 X X
loop(x,500)
end loop
0 0 0 0 4 0
1 0 0 0 4 0
0 8 1 0 X X
1 8 1 0 X X
0 8 0 0 X X
1 8 0 0 X X
loop(x,500)
end loop
0 0 0 0 4 0
1 0 0 0 4 0
0 9 1 0 X X
1 9 1 0 X X
0 9 0 0 X X
1 9 0 0 X X
loop(x,500)
end loop
0 0 0 0 5 0
1 0 0 0 5 0
0 10 1 0 X X
1 10 1 0 X X
0 10 0 0 X X
1 10 0 0 X X
loop(x,500)
end loop
0 0 0 0 5 0
1 0 0 0 5 0
0 11 1 0 X X
1 11 1 0 X X
0 11 0 0 X X
1 11 0 0 X X
loop(x,500)
end loop
0 0 0 0 6 0
1 0 0 0 6 0
0 12 1 0 X X
1 12 1 0 X X
0 12 0 0 X X
1 12 0 0 X X
loop(x,500)
end loop
0 0 0 0 6 0
1 0 0 0 6 0
0 13 1 0 X X
1 13 1 0 X X
0 13 0 0 X X
1 13 0 0 X X
loop(x,500)
end loop
0 0 0 0 7 0
1 0 0 0 7 0
0 14 1 0 X X
1 14 1 0 X X
0 14 0 0 X X
1 14 0 0 X X
loop(x,500)
end loop
0 0 0 0 7 0
1 0 0 0 7 0
0 15 1 0 X X
1 15 1 0 X X
0 15 0 0 X X
1 15 0 0 X X
loop(x,500)
end loop
0 0 0 0 8 0
1 0 0 0 8 0
*/

/* Test case Case5:
clk A input reset mean busy
0 0 0 0 0 0
1 0 0 0 0 0
0 0 0 1 0 0
1 0 0 1 0 0
0 0 0 0 0 0
1 0 0 0 0 0
0 0 1 0 X X
1 0 1 0 X X
0 0 0 0 X X
1 0 0 0 X X
loop(x,500)
end loop
0 0 0 0 0 0
1 0 0 0 0 0
0 0 1 0 X X
1 0 1 0 X X
0 0 0 0 X X
1 0 0 0 X X
loop(x,500)
end loop
0 0 0 0 0 0
1 0 0 0 0 0
0 0 1 0 X X
1 0 1 0 X X
0 0 0 0 X X
1 0 0 0 X X
loop(x,500)
end loop
0 0 0 0 0 0
1 0 0 0 0 0
0 0 1 0 X X
1 0 1 0 X X
0 0 0 0 X X
1 0 0 0 X X
loop(x,500)
end loop
0 0 0 0 0 0
1 0 0 0 0 0
0 0 1 0 X X
1 0 1 0 X X
0 0 0 0 X X
1 0 0 0 X X
loop(x,500)
end loop
0 0 0 0 0 0
1 0 0 0 0 0
0 0 1 0 X X
1 0 1 0 X X
0 0 0 0 X X
1 0 0 0 X X
loop(x,500)
end loop
0 0 0 0 0 0
1 0 0 0 0 0
0 0 1 0 X X
1 0 1 0 X X
0 0 0 0 X X
1 0 0 0 X X
loop(x,500)
end loop
0 0 0 0 0 0
1 0 0 0 0 0
0 0 1 0 X X
1 0 1 0 X X
0 0 0 0 X X
1 0 0 0 X X
loop(x,500)
end loop
0 0 0 0 0 0
1 0 0 0 0 0
0 0 1 0 X X
1 0 1 0 X X
0 0 0 0 X X
1 0 0 0 X X
loop(x,500)
end loop
0 0 0 0 0 0
1 0 0 0 0 0
0 0 1 0 X X
1 0 1 0 X X
0 0 0 0 X X
1 0 0 0 X X
loop(x,500)
end loop
0 0 0 0 0 0
1 0 0 0 0 0
*/
