// Digital circuit p2.dig as structural Verilog
module p2 (
  input  [2:0] In,
  input  clk,
  input  in_10,
  input  in_11,
  output [7:0] Z,
  output b6,
  output b5,
  output b3,
  output b2,
  output b1,
  output b0
);

  wire and_1_out, and_2_out, and_3_out, and_4_out, and_5_out, and_6_out, and_7_out, and_8_out, and_9_out,
       and_10_out, and_11_out, and_12_out, and_13_out, and_14_out, and_15_out, and_16_out, and_17_out,
       and_18_out, and_19_out, and_20_out, and_21_out, and_22_out, and_23_out, not_1_out, not_2_out,
       not_3_out;

  not not_1 (not_1_out, In[2]);
  not not_2 (not_2_out, In[1]);
  not not_3 (not_3_out, In[0]);
  and and_1 (and_1_out, not_1_out, In[1], In[0]);
  and and_2 (and_2_out, In[2], In[1], In[0]);
  and and_3 (and_3_out, not_1_out, not_2_out, In[0]);
  and and_4 (and_4_out, In[2], not_2_out);
  and and_5 (and_5_out, not_2_out, not_3_out);
  and and_6 (and_6_out, In[1], not_3_out);
  and and_7 (and_7_out, In[2], not_2_out, not_3_out);
  and and_8 (and_8_out, In[2], In[1], In[0]);
  and and_9 (and_9_out, not_1_out, not_2_out, In[0]);
  and and_10 (and_10_out, In[1], not_3_out);
  and and_11 (and_11_out, not_1_out, In[1], In[0]);
  and and_12 (and_12_out, not_1_out, not_2_out, In[0]);
  and and_13 (and_13_out, In[2], not_2_out);
  and and_14 (and_14_out, not_1_out, In[1], not_3_out);
  and and_15 (and_15_out, not_1_out, In[1], In[0]);
  and and_16 (and_16_out, In[2], not_2_out);
  and and_17 (and_17_out, not_2_out, not_3_out);
  and and_18 (and_18_out, not_1_out, In[1], not_3_out);
  and and_19 (and_19_out, In[2], not_2_out, not_3_out);
  and and_20 (and_20_out, In[2], In[1], In[0]);
  and and_21 (and_21_out, In[2], not_2_out, not_3_out);
  and and_22 (and_22_out, not_1_out, not_2_out, In[0]);
  and and_23 (and_23_out, In[1], not_3_out);
  or or_1 (b5, and_7_out, and_8_out, and_9_out, and_10_out);
  or or_2 (b3, and_11_out, and_12_out, and_13_out);
  or or_3 (b2, and_14_out, and_15_out, and_16_out, and_17_out);
  or or_4 (b1, and_18_out, and_19_out, and_20_out);
  or or_5 (b0, and_21_out, and_22_out, and_23_out);
  or or_6 (b6, and_1_out, and_2_out, and_3_out, and_4_out, and_5_out, and_6_out);
  Terminal terminal_1 (.D({in_11, b6, b5, in_10, b3, b2, b1, b0}), .C(clk), .en(1'b1));

  assign Z = {in_11, b6, b5, in_10, b3, b2, b1, b0};

  // Other names for the same wires on the sheet: _0 = b0; _1 = b1; _2 = b2; _3 = b3; _4 = in_10; _5 = b5; _6 = b6;
  //   _7 = in_11
endmodule
