// Digital circuit 01.dig as structural Verilog
module _01 (
  input  [3:0] In,
  input  [1:0] Selector,
  output out_3,
  output out_4,
  output out_5,
  output out_6
);

  wire [3:0] _642_3code_1_cyclic, _2421code_1_cyclic, cyclic_1_cyclic, excess_3_1_excess_3_out;

  Excess_3 excess_3_1 (.IN(In), .Excess_3_OUT(excess_3_1_excess_3_out));
  Cyclic cyclic_1 (.IN(In), .Cyclic(cyclic_1_cyclic));
  _2421Code _2421code_1 (.IN(In), .Cyclic(_2421code_1_cyclic));
  _642_3Code _642_3code_1 (.IN(In), .Cyclic(_642_3code_1_cyclic));
  Multiplexer #(.Bits(4), .Selector_Bits(2)) multiplexer_1 (
    .sel(Selector), .in_0(excess_3_1_excess_3_out), .in_1(cyclic_1_cyclic), .in_2(_2421code_1_cyclic),
    .in_3(_642_3code_1_cyclic), .out({out_3, out_4, out_5, out_6}));
endmodule
