// Digital circuit 02.dig as structural Verilog
module _02 (
  input  [6:0] In,
  output [6:0] Output,
  output m4,
  output m3,
  output m2,
  output p3,
  output m1,
  output p2,
  output p1,
  output [3:0] Output_4_BITS
);

  wire hammingbitsxor_1_c1, hammingbitsxor_1_c2, hammingbitsxor_1_c3;
  wire [6:0] invertindex_1_convert_sig;

  HammingBitsXOR hammingbitsxor_1 (
    .p1(In[6]), .p2(In[5]), .m1(In[4]), .p3(In[3]), .m2(In[2]), .m3(In[1]), .m4(In[0]),
    .C1(hammingbitsxor_1_c1), .C2(hammingbitsxor_1_c2), .C3(hammingbitsxor_1_c3));
  invertIndex invertindex_1 (
    .C1(hammingbitsxor_1_c1), .C2(hammingbitsxor_1_c2), .C3(hammingbitsxor_1_c3),
    .CONVERT_SIG(invertindex_1_convert_sig));
  INVERT_BITer invert_biter_1 (
    .BitToInvert(invertindex_1_convert_sig), .m4(In[0]), .m3(In[1]), .m2(In[2]), .p3(In[3]), .m1(In[4]),
    .p2(In[5]), .p1(In[6]), .OUTPUTto({Output[6:5], m1, Output[3], m2, m3, m4}));

  assign {Output[4], Output[2:0]} = {m1, m2, m3, m4};
  assign Output_4_BITS = {m1, m2, m3, m4};
  assign p1 = Output[6];
  assign p2 = Output[5];
  assign p3 = Output[3];
endmodule
