// Digital circuit bitinvertSwitch.dig as structural Verilog
module bitinvertSwitch (
  input  BIT,
  input  INVERT_BOOL,
  output Y
);

  wire and_1_out, and_2_out, not_1_out, not_2_out;

  not not_1 (not_1_out, BIT);
  not not_2 (not_2_out, INVERT_BOOL);
  and and_1 (and_1_out, not_1_out, INVERT_BOOL);
  and and_2 (and_2_out, BIT, not_2_out);
  or or_1 (Y, and_1_out, and_2_out);
endmodule
