// Digital circuit invertIndex.dig as structural Verilog
module invertIndex (
  input  C1,
  input  C2,
  input  C3,
  output [6:0] CONVERT_SIG
);

  wire not_1_out, not_2_out, not_3_out;

  not not_1 (not_1_out, C1);
  not not_2 (not_2_out, C2);
  not not_3 (not_3_out, C3);
  and and_1 (CONVERT_SIG[6], not_1_out, not_2_out, C3);
  and and_2 (CONVERT_SIG[5], not_1_out, C2, not_3_out);
  and and_3 (CONVERT_SIG[4], not_1_out, C2, C3);
  and and_4 (CONVERT_SIG[3], C1, not_2_out, not_3_out);
  and and_5 (CONVERT_SIG[2], C1, not_2_out, C3);
  and and_6 (CONVERT_SIG[1], C1, C2, not_3_out);
  and and_7 (CONVERT_SIG[0], C1, C2, C3);
endmodule
