// Digital circuit 41Mux.dig as structural Verilog
module _41Mux (
  input  A,
  input  B,
  input  C,
  input  D,
  input  S1,
  input  S0,
  output OUT
);

  wire and_1_out, and_2_out, and_3_out, and_4_out, not_1_out, not_2_out, not_3_out, not_4_out, not_5_out,
       not_6_out;

  not not_1 (not_1_out, A);
  not not_2 (not_2_out, B);
  not not_3 (not_3_out, C);
  not not_4 (not_4_out, D);
  not not_5 (not_5_out, S1);
  not not_6 (not_6_out, S0);
  and and_1 (and_1_out, not_1_out, not_2_out, not_3_out, D, not_5_out, not_6_out);
  and and_2 (and_2_out, not_1_out, not_2_out, C, not_4_out, not_5_out, S0);
  and and_3 (and_3_out, not_1_out, B, not_3_out, not_4_out, S1, not_6_out);
  and and_4 (and_4_out, A, not_2_out, not_3_out, not_4_out, S1, S0);
  or or_1 (OUT, and_1_out, and_2_out, and_3_out, and_4_out);
endmodule
