// Digital circuit HammingBitsXOR.dig as structural Verilog
module HammingBitsXOR (
  input  p1,
  input  p2,
  input  m1,
  input  p3,
  input  m2,
  input  m3,
  input  m4,
  output C1,
  output C2,
  output C3
);

  xor xor_1 (C1, p3, m2, m3, m4);
  xor xor_2 (C2, p2, m1, m3, m4);
  xor xor_3 (C3, p1, m1, m2, m4);
endmodule
