// Digital circuit INVERT BITer.dig as structural Verilog
module INVERT_BITer (
  input  [6:0] BitToInvert,
  input  m4,
  input  m3,
  input  m2,
  input  p3,
  input  m1,
  input  p2,
  input  p1,
  output [6:0] OUTPUTto
);

  bitinvertSwitch bitinvertswitch_1 (.BIT(m4), .INVERT_BOOL(BitToInvert[0]), .Y(OUTPUTto[0]));
  bitinvertSwitch bitinvertswitch_2 (.BIT(m3), .INVERT_BOOL(BitToInvert[1]), .Y(OUTPUTto[1]));
  bitinvertSwitch bitinvertswitch_3 (.BIT(m2), .INVERT_BOOL(BitToInvert[2]), .Y(OUTPUTto[2]));
  bitinvertSwitch bitinvertswitch_4 (.BIT(p3), .INVERT_BOOL(BitToInvert[3]), .Y(OUTPUTto[3]));
  bitinvertSwitch bitinvertswitch_5 (.BIT(m1), .INVERT_BOOL(BitToInvert[4]), .Y(OUTPUTto[4]));
  bitinvertSwitch bitinvertswitch_6 (.BIT(p2), .INVERT_BOOL(BitToInvert[5]), .Y(OUTPUTto[5]));
  bitinvertSwitch bitinvertswitch_7 (.BIT(p1), .INVERT_BOOL(BitToInvert[6]), .Y(OUTPUTto[6]));
endmodule
