// Digital circuit 4bit41mux.dig as structural Verilog
module _4bit41mux (
  input  _642_3Code,
  input  [3:0] _2421Code,
  input  [3:0] Cyclic,
  input  [3:0] Excess_3
);

  _41Mux _41mux_1 ();  // open: A, B, C, D, S1, S0, OUT
  _41Mux _41mux_2 ();  // open: A, B, C, D, S1, S0, OUT
  _41Mux _41mux_3 ();  // open: A, B, C, D, S1, S0, OUT
  _41Mux _41mux_4 ();  // open: A, B, C, D, S1, S0, OUT
endmodule
