// Digital circuit 642-3Code.dig as structural Verilog
module _642_3Code (
  input  [3:0] IN,
  output [3:0] Cyclic
);

  wire and_1_out, and_2_out, and_3_out, and_4_out, and_5_out, and_6_out, and_7_out, not_1_out, not_2_out,
       not_3_out;

  not not_1 (not_1_out, IN[2]);
  not not_2 (not_2_out, IN[1]);
  not not_3 (not_3_out, IN[0]);
  and and_1 (and_1_out, IN[2], IN[0]);
  and and_2 (and_2_out, IN[1], IN[0]);
  and and_3 (and_3_out, not_1_out, not_2_out, IN[0]);
  and and_4 (and_4_out, IN[2], not_3_out);
  and and_5 (and_5_out, IN[2], IN[1]);
  and and_6 (and_6_out, IN[2], not_2_out, IN[0]);
  and and_7 (and_7_out, IN[1], not_3_out);
  or or_1 (Cyclic[3], IN[3], and_1_out, and_2_out);
  or or_2 (Cyclic[2], and_3_out, and_4_out, and_5_out);
  or or_3 (Cyclic[1], IN[3], and_6_out, and_7_out);

  assign Cyclic[0] = IN[0];
endmodule
