// Digital circuit Cyclic.dig as structural Verilog
module Cyclic (
  input  [3:0] IN,
  output [3:0] Cyclic
);

  wire and_1_out, and_2_out, and_3_out, and_4_out, not_1_out, not_2_out, not_3_out;

  not not_1 (not_1_out, IN[2]);
  not not_2 (not_2_out, IN[1]);
  not not_3 (not_3_out, IN[0]);
  or or_1 (Cyclic[2], IN[3], IN[2]);
  and and_1 (and_1_out, not_1_out, IN[1]);
  and and_2 (and_2_out, IN[2], not_2_out);
  and and_3 (and_3_out, not_2_out, IN[0]);
  and and_4 (and_4_out, IN[1], not_3_out);
  or or_2 (Cyclic[1], and_1_out, and_2_out);
  or or_3 (Cyclic[0], and_3_out, and_4_out);

  assign Cyclic[3] = IN[3];
endmodule
