// Digital circuit selector.dig as structural Verilog
module selector (
  input  [3:0] Excess_3,
  input  Cyclic,
  input  [1:0] Selector,
  input  _2_4_2_1_code,
  input  _6_4_2__3_code,
  input  [1:0] niga,
  output Z
);

  wire and_2_out, and_3_out, and_4_out, not_5_out;
  wire [1:0] or_1_out;
  wire [3:0] and_1_out, not_6_out, not_7_out;

  // Not not_1 has open pins: in=Excess_3[0], out=open
  // Not not_2 has open pins: in=Cyclic, out=open
  // Not not_3 has open pins: in=_2_4_2_1_code, out=open
  // Not not_4 has open pins: in=_6_4_2__3_code, out=open
  not not_5 (not_5_out, niga[0]);
  or or_1 (or_1_out[0], not_5_out, niga[0]);
  not not_6 (not_6_out[0], Selector[1]);
  not not_7 (not_7_out[0], Selector[0]);
  assign and_1_out = Excess_3 & not_6_out & not_7_out;  // And and_1, 4 bits wide
  and and_2 (and_2_out, Cyclic, not_6_out[0], Selector[0]);
  and and_3 (and_3_out, _2_4_2_1_code, Selector[1], not_7_out[0]);
  and and_4 (and_4_out, _6_4_2__3_code, Selector[1], Selector[0]);
  or or_2 (Z, and_1_out[0], and_2_out, and_3_out, and_4_out);
  // Pins of 1 and 4 bits meet at Excess_3
  // Pins of 1 and 3 bits meet at {or_1_out, Selector[1]}
  // Pins of 1 and 4 bits meet at not_6_out
  // Pins of 1 and 4 bits meet at not_7_out
  // Pins of 1 and 4 bits meet at and_1_out
  // Pins of 1 and 2 bits meet at or_1_out
  // Pins of 1 and 2 bits meet at niga
endmodule
