// Digital circuit Template.dig as structural Verilog
module Template (
  input  [7:0] In,
  output [8:0] Output,
  output useless_nub
);

  wire [8:0] not_1_out;

  assign not_1_out = ~{1'b0, In};  // Not not_1, 9 bits wide
  Add #(.Bits(9)) add_1 (.a(not_1_out), .b(9'h1), .c_i(1'b0), .s(Output), .c_o(useless_nub));
endmodule
