// Digital circuit Template.dig as structural Verilog
module Template (
  input  [3:0] A,
  input  [3:0] B,
  input  [2:0] S,
  input  M,
  input  C,
  output [3:0] F,
  output Cout
);

  wire arithmetic_functions_1_of;
  wire [3:0] arithmetic_functions_1_out, logicalfunctions_1_out;

  LogicalFunctions logicalfunctions_1 (.A(A), .B(B), .Sel(S), .OUT(logicalfunctions_1_out));
  arithmetic_functions arithmetic_functions_1 (
    .A(A), .B(B), .C(C), .Sel(S), .OUT(arithmetic_functions_1_out), .OF(arithmetic_functions_1_of));
  Multiplexer #(.Bits(4)) multiplexer_1 (
    .sel(M), .in_0(logicalfunctions_1_out), .in_1(arithmetic_functions_1_out), .out(F));
  Multiplexer multiplexer_2 (.sel(M), .in_0(1'b0), .in_1(arithmetic_functions_1_of), .out(Cout));

  // Other names for the same wires on the sheet: eminem = M
endmodule
