// Digital circuit 4-BitsAdder-inator.dig as structural Verilog
module _4_BitsAdder_inator (
  input  [3:0] A,
  input  [3:0] B,
  output [3:0] Sum,
  output OF
);

  wire add_1_c_o, add_2_c_o, add_3_c_o, add_4_c_o;

  Add add_1 (.a(A[0]), .b(B[0]), .c_i(1'b0), .s(Sum[0]), .c_o(add_1_c_o));
  Add add_2 (.a(A[1]), .b(B[1]), .c_i(add_1_c_o), .s(Sum[1]), .c_o(add_2_c_o));
  Add add_3 (.a(A[2]), .b(B[2]), .c_i(add_2_c_o), .s(Sum[2]), .c_o(add_3_c_o));
  Add add_4 (.a(A[3]), .b(B[3]), .c_i(add_3_c_o), .s(Sum[3]), .c_o(add_4_c_o));
  xor xor_1 (OF, add_3_c_o, add_4_c_o);
endmodule
