// Digital circuit ArithmeticFunction.dig as structural Verilog
module ArithmeticFunction (
  input  [3:0] A,
  input  [3:0] B,
  input  C,
  input  [2:0] Sel,
  input  C_2,
  output [3:0] OUT,
  output OF
);

  wire _4_bitsadder_inator_1_of, _4_bitsadder_inator_2_of, _4_bitsadder_inator_3_of,
       _4_bitsadder_inator_4_of, _4_bitsadder_inator_5_of, _4_bitsadder_inator_6_of, multiplexer_2_out,
       or_1_out;
  wire [3:0] _4_bitsadder_inator_1_sum, _4_bitsadder_inator_2_sum, _4_bitsadder_inator_3_sum,
       _4_bitsadder_inator_4_sum, _4_bitsadder_inator_5_sum, _4_bitsadder_inator_6_sum, multiplexer_1_out,
       two_scompliment_inator_1_out, two_scompliment_inator_2_out;

  TWO_sCompliment_inator two_scompliment_inator_1 (.In(B), .Out(two_scompliment_inator_1_out));
  TWO_sCompliment_inator two_scompliment_inator_2 (.In(A), .Out(two_scompliment_inator_2_out));
  _4_BitsAdder_inator _4_bitsadder_inator_1 (
    .A(A), .B(4'b1111), .Sum(_4_bitsadder_inator_1_sum), .OF(_4_bitsadder_inator_1_of));
  _4_BitsAdder_inator _4_bitsadder_inator_2 (
    .A(A), .B(B), .Sum(_4_bitsadder_inator_2_sum), .OF(_4_bitsadder_inator_2_of));
  _4_BitsAdder_inator _4_bitsadder_inator_3 (
    .A(A), .B(two_scompliment_inator_1_out), .Sum(_4_bitsadder_inator_3_sum), .OF(_4_bitsadder_inator_3_of));
  _4_BitsAdder_inator _4_bitsadder_inator_4 (
    .A(two_scompliment_inator_2_out), .B(4'b1111), .Sum(_4_bitsadder_inator_4_sum),
    .OF(_4_bitsadder_inator_4_of));
  _4_BitsAdder_inator _4_bitsadder_inator_5 (
    .A(_4_bitsadder_inator_3_sum), .B(4'b1111), .Sum(_4_bitsadder_inator_5_sum), .OF(_4_bitsadder_inator_5_of));
  or or_1 (or_1_out, _4_bitsadder_inator_5_of, _4_bitsadder_inator_3_of);
  Multiplexer #(.Selector_Bits(3), .Bits(4)) multiplexer_1 (
    .sel(Sel), .in_0(A), .in_1(_4_bitsadder_inator_1_sum), .in_2(_4_bitsadder_inator_2_sum),
    .in_3(_4_bitsadder_inator_5_sum), .in_4(_4_bitsadder_inator_4_sum), .in_5(B), .in_6({A[2:0], 1'b0}),
    .in_7({1'b0, A[3:1]}), .out(multiplexer_1_out));
  _4_BitsAdder_inator _4_bitsadder_inator_6 (
    .A(multiplexer_1_out), .B(4'b0001), .Sum(_4_bitsadder_inator_6_sum), .OF(_4_bitsadder_inator_6_of));
  Multiplexer #(.Selector_Bits(3)) multiplexer_2 (
    .sel(Sel), .in_0(1'b0), .in_1(_4_bitsadder_inator_1_of), .in_2(_4_bitsadder_inator_2_of),
    .in_3(or_1_out), .in_4(_4_bitsadder_inator_4_of), .in_5(1'b0), .in_6(1'b0), .in_7(1'b0),
    .out(multiplexer_2_out));
  Multiplexer multiplexer_3 (.sel(C_2), .in_0(multiplexer_2_out), .in_1(_4_bitsadder_inator_6_of), .out(OF));
  Multiplexer #(.Bits(4)) multiplexer_4 (
    .sel(C), .in_0(multiplexer_1_out), .in_1(_4_bitsadder_inator_6_sum), .out(OUT));
endmodule
