// Digital circuit LogicalFunctions.dig as structural Verilog
module LogicalFunctions (
  input  [3:0] A,
  input  [3:0] B,
  input  [2:0] Sel,
  output [3:0] OUT
);

  wire [3:0] and_1_out, and_2_out, nand_1_out, nor_1_out, not_1_out, or_1_out, xnor_1_out;

  assign not_1_out = ~A;  // Not not_1, 4 bits wide
  assign nand_1_out = ~(A & B);  // NAnd nand_1, 4 bits wide
  assign nor_1_out = ~(A | B);  // NOr nor_1, 4 bits wide
  assign xnor_1_out = ~(A ^ B);  // XNOr xnor_1, 4 bits wide
  assign and_1_out = A & B;  // And and_1, 4 bits wide
  assign or_1_out = A | B;  // Or or_1, 4 bits wide
  assign and_2_out = A & ~B;  // And and_2, 4 bits wide
  Multiplexer #(.Selector_Bits(3), .Bits(4)) multiplexer_1 (
    .sel(Sel), .in_0(not_1_out), .in_1(nand_1_out), .in_2(nor_1_out), .in_3(xnor_1_out), .in_4(and_1_out),
    .in_5(or_1_out), .in_6(and_2_out), .in_7(A), .out(OUT));
endmodule
