// Digital circuit TWO'sCompliment-inator.dig as structural Verilog
module TWO_sCompliment_inator (
  input  [3:0] In,
  output [3:0] Out
);

  wire [3:0] not_1_out;

  assign not_1_out = ~In;  // Not not_1, 4 bits wide
  Add #(.Bits(4)) Plus_One_inator (.a(not_1_out), .b(4'b0001), .c_i(1'b0), .s(Out));  // open: c_o
endmodule
