// Digital circuit 64_1.dig as structural Verilog
module _64_1 (
  input  [2:0] in_1,
  input  [2:0] in_2
);

  wire [0:0] comparator_1_gt;
  wire [3:0] add_1_s;

  Add #(.Bits(4)) add_1 (.a({1'b0, in_1}), .b({1'b0, in_2}), .c_i(1'b0), .s(add_1_s));  // open: c_o
  Comparator #(.Bits(4)) comparator_1 (.a(add_1_s), .b(4'b0110), .gt(comparator_1_gt[0]));  // open: eq, lt
  Seven_Seg_Hex seven_seg_hex_1 (.d({3'b000, comparator_1_gt[0]}), .dp(1'b0));
endmodule
