// Digital circuit Digital_Quiz1_Example1.dig as structural Verilog
module Digital_Quiz1_Example1 (
  input  S1,
  input  S2,
  input  S3,
  input  S4,
  input  S5,
  input  S6,
  input  S7,
  input  S8,
  output [2:0] g1,
  output [1:0] g2,
  output out_11
);

  BitCount #(.Bits(5)) bitcount_1 (.in({S5, S4, S3, S2, S1}), .out(g1));
  BitCount #(.Bits(3)) bitcount_2 (.in({S8, S7, S6}), .out(g2));
  Comparator #(.Bits(3)) comparator_1 (.a(g1), .b({1'b0, g2}), .eq(out_11));  // open: gt, lt
endmodule
